// Logisim project CPU.circ as structural Verilog: 28 circuits, main circuit cpu
module Processor (
  input  in_1
);

  wire and_1_out, and_2_out, and_3_out, and_4_out, binary_to_bcd_1_sup_out, binary_to_bcd_2_sup_out,
       binary_to_bcd_3_sup_out, binary_to_bcd_4_sup_out, binary_to_bcd_5_sup_out, binary_to_bcd_6_sup_out,
       binary_to_bcd_7_sup_out, binary_to_bcd_8_sup_out, binary_to_bcd_9_sup_out, businterface_1_bm0,
       businterface_1_bm1, businterface_1_bm2, businterface_1_bm3, businterface_1_nrw, businterface_1_strobe,
       button_1_out, button_2_out, CLK, clock_1_out, comparator_1_eq, comparator_2_eq, comparator_3_eq,
       controlstatusregisters_1_eie, controlstatusregisters_1_ill, EAL, EPL, EQ, fetchunit_1_ldsx,
       fetchunit_1_load0, fetchunit_1_load1, fetchunit_1_pce, fetchunit_1_store0, fetchunit_1_store1,
       instructiondecoder_1_brk, instructiondecoder_1_csr_bit, instructiondecoder_1_csr_clr,
       instructiondecoder_1_csr_en, instructiondecoder_1_csr_sel, instructiondecoder_1_hold,
       instructiondecoder_1_ill, instructiondecoder_1_ld0, instructiondecoder_1_ld1,
       instructiondecoder_1_ret, instructiondecoder_1_st0, instructiondecoder_1_st1, instructiondecoder_1_sx,
       instructiondecoder_1_sys, instructiondecoder_1_wfi, interruptcontroller_1_rdy,
       interruptcontroller_1_trap, IRG, IRQ, JMP, LCS, LDR, LNK, LT, LTU, not_1_out, not_2_out, OPI, RDY,
       REL, RST, SET;
  wire [4:0] RD, RS1, RS2, SEL;
  wire [11:0] instructiondecoder_1_csri;
  wire [13:0] businterface_1_a_2;
  wire [15:0] businterface_1_a, register_1_q, register_2_q;
  wire [31:0] ALU, binary_to_bcd_2_vout, binary_to_bcd_3_vout, binary_to_bcd_4_vout, binary_to_bcd_5_vout,
       binary_to_bcd_6_vout, binary_to_bcd_7_vout, binary_to_bcd_8_vout, binary_to_bcd_9_vout,
       binary_to_bcd_10_vout, bit_extender_1_out, bit_extender_2_out, controlstatusregisters_1_epc,
       controlstatusregisters_1_isr, CSR, fetchunit_1_addr, fetchunit_1_instr, IMM,
       instructiondecoder_1_csr_imm, interruptcontroller_1_cause, MDI, NPC, PC, ram_1_data, REF,
       register_3_q, RES, rom_1_data, RX, RY, shifter_1_out, shifter_2_out;

  not not_1 (not_1_out, not_2_out);
  assign bit_extender_1_out = {{2{businterface_1_a_2[13]}}, {businterface_1_a_2, businterface_1_a}};  // Bit_Extender bit_extender_1
  _7_Segment_Display u_7_segment_display_1 ();  // open: g, f, a, b, e, d, c, dp
  _7_Segment_Display u_7_segment_display_2 ();  // open: g, f, a, b, e, d, c, dp
  // BCD_to_7_Segment_decoder bcd_to_7_segment_decoder_1: pin names not known
  // BCD_to_7_Segment_decoder bcd_to_7_segment_decoder_2: pin names not known
  binary_to_bcd binary_to_bcd_1 (
    .SUP_OUT(binary_to_bcd_1_sup_out), .VIN(binary_to_bcd_2_vout), .SUP_IN(1'b1), .SUP_0(1'b1));  // open: VOUT, DIGIT
  binary_to_bcd binary_to_bcd_2 (
    .VOUT(binary_to_bcd_2_vout), .SUP_OUT(binary_to_bcd_2_sup_out), .VIN(binary_to_bcd_3_vout),
    .SUP_IN(binary_to_bcd_1_sup_out), .SUP_0(1'b1));  // open: DIGIT
  Comparator #(.width(14)) comparator_1 (.a(businterface_1_a_2), .b({14{1'b1}}), .eq(comparator_1_eq));  // open: gt, lt
  Comparator #(.width(14)) comparator_2 (.a(businterface_1_a_2), .b(14'h200), .eq(comparator_2_eq));  // open: gt, lt
  and and_1 (and_1_out, not_1_out, comparator_2_eq);
  and and_2 (and_2_out, comparator_2_eq, not_2_out);
  Shifter #(.width(32)) shifter_1 (.in(bit_extender_1_out), .\dist (5'b00010), .out(shifter_1_out));
  _7_Segment_Display u_7_segment_display_3 ();  // open: g, f, a, b, e, d, c, dp
  // BCD_to_7_Segment_decoder bcd_to_7_segment_decoder_3: pin names not known
  binary_to_bcd binary_to_bcd_3 (
    .VOUT(binary_to_bcd_3_vout), .SUP_OUT(binary_to_bcd_3_sup_out), .VIN(binary_to_bcd_4_vout),
    .SUP_IN(binary_to_bcd_2_sup_out), .SUP_0(1'b1));  // open: DIGIT
  ROM #(.addrWidth(16), .dataWidth(32)) rom_1 (.addr(register_1_q), .data(rom_1_data));
  Register #(.trigger("high"), .width(16)) register_1 (
    .D(businterface_1_a), .Q(register_1_q), .clk(comparator_1_eq));  // open: en, clr
  RAM #(.addrWidth(16), .asyncread("true"), .byteenables("byteEnables"), .dataWidth(32), .databus("bidir"), .trigger("falling")) ram_1 (
    .addr(register_2_q), .we(and_1_out), .oe(and_2_out), .clk(businterface_1_strobe), .data(ram_1_data),
    .be3(businterface_1_bm3), .be2(businterface_1_bm2), .be1(businterface_1_bm1), .be0(businterface_1_bm0));
  Register #(.trigger("high"), .width(16)) register_2 (
    .D(businterface_1_a), .Q(register_2_q), .clk(comparator_2_eq));  // open: en, clr
  and and_3 (and_3_out, ~not_2_out, comparator_3_eq);  // AND_Gate
  Comparator #(.width(32)) comparator_3 (.a(shifter_1_out), .b(32'hc0008000), .eq(comparator_3_eq));  // open: gt, lt
  _7_Segment_Display u_7_segment_display_4 ();  // open: g, f, a, b, e, d, c, dp
  _7_Segment_Display u_7_segment_display_5 ();  // open: g, f, a, b, e, d, c, dp
  // BCD_to_7_Segment_decoder bcd_to_7_segment_decoder_4: pin names not known
  // BCD_to_7_Segment_decoder bcd_to_7_segment_decoder_5: pin names not known
  binary_to_bcd binary_to_bcd_4 (
    .VOUT(binary_to_bcd_4_vout), .SUP_OUT(binary_to_bcd_4_sup_out), .VIN(binary_to_bcd_5_vout),
    .SUP_IN(binary_to_bcd_3_sup_out), .SUP_0(1'b1));  // open: DIGIT
  binary_to_bcd binary_to_bcd_5 (
    .VOUT(binary_to_bcd_5_vout), .SUP_OUT(binary_to_bcd_5_sup_out), .VIN(binary_to_bcd_6_vout),
    .SUP_IN(binary_to_bcd_4_sup_out), .SUP_0(1'b1));  // open: DIGIT
  Register #(.width(32)) register_3 (
    .D(ram_1_data), .en(and_3_out), .clk(businterface_1_strobe), .Q(register_3_q));  // open: clr
  _7_Segment_Display u_7_segment_display_6 ();  // open: g, f, a, b, e, d, c, dp
  _7_Segment_Display u_7_segment_display_7 ();  // open: g, f, a, b, e, d, c, dp
  // BCD_to_7_Segment_decoder bcd_to_7_segment_decoder_6: pin names not known
  // BCD_to_7_Segment_decoder bcd_to_7_segment_decoder_7: pin names not known
  binary_to_bcd binary_to_bcd_6 (
    .VOUT(binary_to_bcd_6_vout), .SUP_OUT(binary_to_bcd_6_sup_out), .VIN(binary_to_bcd_7_vout),
    .SUP_IN(binary_to_bcd_5_sup_out), .SUP_0(1'b1));  // open: DIGIT
  _7_Segment_Display u_7_segment_display_8 ();  // open: g, f, a, b, e, d, c, dp
  // BCD_to_7_Segment_decoder bcd_to_7_segment_decoder_8: pin names not known
  binary_to_bcd binary_to_bcd_7 (
    .VOUT(binary_to_bcd_7_vout), .SUP_OUT(binary_to_bcd_7_sup_out), .VIN(binary_to_bcd_8_vout),
    .SUP_IN(binary_to_bcd_6_sup_out), .SUP_0(1'b1));  // open: DIGIT
  binary_to_bcd binary_to_bcd_8 (
    .VOUT(binary_to_bcd_8_vout), .SUP_OUT(binary_to_bcd_8_sup_out), .VIN(binary_to_bcd_9_vout),
    .SUP_IN(binary_to_bcd_7_sup_out), .SUP_0(1'b1));  // open: DIGIT
  assign bit_extender_2_out = {{2{businterface_1_a_2[13]}}, {businterface_1_a_2, businterface_1_a}};  // Bit_Extender bit_extender_2
  assign ram_1_data = and_4_out ? rom_1_data : 32'bz;  // Controlled_Buffer controlled_buffer_1
  and and_4 (and_4_out, comparator_1_eq, not_2_out);
  _7_Segment_Display u_7_segment_display_9 ();  // open: g, f, a, b, e, d, c, dp
  _7_Segment_Display u_7_segment_display_10 ();  // open: g, f, a, b, e, d, c, dp
  // BCD_to_7_Segment_decoder bcd_to_7_segment_decoder_9: pin names not known
  // BCD_to_7_Segment_decoder bcd_to_7_segment_decoder_10: pin names not known
  binary_to_bcd binary_to_bcd_9 (
    .VOUT(binary_to_bcd_9_vout), .SUP_OUT(binary_to_bcd_9_sup_out), .VIN(binary_to_bcd_10_vout),
    .SUP_IN(binary_to_bcd_8_sup_out), .SUP_0(1'b1));  // open: DIGIT
  binary_to_bcd binary_to_bcd_10 (
    .VOUT(binary_to_bcd_10_vout), .VIN(register_3_q), .SUP_IN(binary_to_bcd_9_sup_out), .SUP_0(1'b0));  // open: SUP_OUT, DIGIT
  // Probe on shifter_2_out
  Shifter #(.width(32)) shifter_2 (.in(bit_extender_2_out), .\dist (5'b00010), .out(shifter_2_out));
  // Probe on ram_1_data
  BusInterface businterface_1 (
    .DIN(MDI), .A({businterface_1_a_2, businterface_1_a}), .STROBE(businterface_1_strobe), .EALIGN(EAL),
    .BM0(businterface_1_bm0), .BM1(businterface_1_bm1), .BM2(businterface_1_bm2), .BM3(businterface_1_bm3),
    .nRW(businterface_1_nrw), .DO(ram_1_data), .DI(ram_1_data), .DOUT(RY), .RST(RST), .CLK(CLK),
    .LDSX(fetchunit_1_ldsx), .LOAD0(fetchunit_1_load0), .LOAD1(fetchunit_1_load1),
    .STORE0(fetchunit_1_store0), .STORE1(fetchunit_1_store1), .ADDR(fetchunit_1_addr));
  not not_2 (not_2_out, businterface_1_nrw);
  // register_file register_file_1: pin names not known; wires that end beside it: RES, RD, RS1, RS2, CLK, RX, RY
  FetchUnit fetchunit_1 (
    .INSTR(fetchunit_1_instr), .ADDR(fetchunit_1_addr), .PC(PC), .GRANT(IRG), .PCE(fetchunit_1_pce),
    .LDSX(fetchunit_1_ldsx), .LOAD0(fetchunit_1_load0), .LOAD(LDR), .LOAD1(fetchunit_1_load1),
    .STORE0(fetchunit_1_store0), .STORE1(fetchunit_1_store1), .EMA(ALU), .PC_IN(NPC), .CLK(CLK), .IRQ(IRQ),
    .HOLD(instructiondecoder_1_hold), .SX(instructiondecoder_1_sx), .LD0(instructiondecoder_1_ld0),
    .LD1(instructiondecoder_1_ld1), .ST0(instructiondecoder_1_st0), .ST1(instructiondecoder_1_st1), .DIN(MDI));
  ProgramCounter programcounter_1 (.EALIGN(EPL), .PC(NPC), .PCE(fetchunit_1_pce), .CLK(CLK), .JMP(SET), .ADDR(REF));
  InstructionDecoder instructiondecoder_1 (
    .RS2(RS2), .OPIMM(OPI), .BRANCH(JMP), .PCREL(REL), .ILL(instructiondecoder_1_ill),
    .WFI(instructiondecoder_1_wfi), .RET(instructiondecoder_1_ret), .BRK(instructiondecoder_1_brk),
    .SYS(instructiondecoder_1_sys), .CSRI(instructiondecoder_1_csri), .CSR_EN(instructiondecoder_1_csr_en),
    .IMM(IMM), .CSR_IMM(instructiondecoder_1_csr_imm), .LINK(LNK), .SX(instructiondecoder_1_sx),
    .LD0(instructiondecoder_1_ld0), .LD1(instructiondecoder_1_ld1), .ST0(instructiondecoder_1_st0),
    .ST1(instructiondecoder_1_st1), .ALU_OP(SEL), .RD(RD), .RS1(RS1), .HOLD(instructiondecoder_1_hold),
    .CSR_SEL(instructiondecoder_1_csr_sel), .CSR_BIT(instructiondecoder_1_csr_bit),
    .CSR_CLR(instructiondecoder_1_csr_clr), .INSTR(fetchunit_1_instr), .EQ(EQ), .LT(LT), .LTU(LTU),
    .RDY(interruptcontroller_1_rdy), .CLK(CLK), .RST(RST));
  ResultMux resultmux_1 (.RES(RES), .ALU(ALU), .NPC(NPC), .MDI(MDI), .CSR(CSR), .LINK(LNK), .LOAD(LDR), .LDCSR(LCS));
  Clock clock_1 (.out(clock_1_out));
  xor xor_1 (CLK, clock_1_out, button_1_out);
  Button button_1 (.out(button_1_out));
  not not_3 (RST, in_1);
  InterruptController interruptcontroller_1 (
    .TRAP(interruptcontroller_1_trap), .SET(SET), .RDY(interruptcontroller_1_rdy), .IRQ(IRQ),
    .CAUSE(interruptcontroller_1_cause), .REF(REF), .TRIG(button_2_out), .GRANT(IRG), .CLK(CLK), .ALU(ALU),
    .EPC(controlstatusregisters_1_epc), .ISR(controlstatusregisters_1_isr), .RST(RST),
    .RET(instructiondecoder_1_ret), .JMP(JMP), .WFI(instructiondecoder_1_wfi), .RDY_IN(RDY),
    .EIE(controlstatusregisters_1_eie), .SYS(instructiondecoder_1_sys), .BRK(instructiondecoder_1_brk),
    .LDR(LDR), .EAM(EAL), .EPL(EPL), .ILL(controlstatusregisters_1_ill));
  Button button_2 (.out(button_2_out));
  ArithmeticLogicUnit arithmeticlogicunit_1 (
    .R(ALU), .RDY(RDY), .EQ(EQ), .LT(LT), .LTU(LTU), .SEL(SEL), .A(RX), .PC(PC), .PCREL(REL), .B(RY),
    .IMM(IMM), .OPIMM(OPI), .CLK(CLK));
  ControlStatusRegisters controlstatusregisters_1 (
    .ISR(controlstatusregisters_1_isr), .ILL(controlstatusregisters_1_ill),
    .EPC(controlstatusregisters_1_epc), .CSR_OUT(CSR), .EIE(controlstatusregisters_1_eie), .LDCSR(LCS),
    .RST(RST), .ILL_IN(instructiondecoder_1_ill), .CLR(instructiondecoder_1_csr_clr),
    .IRET(instructiondecoder_1_ret), .OPIMM(instructiondecoder_1_csr_sel), .CSR(instructiondecoder_1_csri),
    .RX(RX), .IMM(instructiondecoder_1_csr_imm), .BIT(instructiondecoder_1_csr_bit),
    .CSE(instructiondecoder_1_csr_en), .PC(PC), .CAUSE_IN(interruptcontroller_1_cause),
    .TRAP(interruptcontroller_1_trap), .CLK(CLK));

  // Notes on the sheet:
  //   contents of rom_1 (hex, n*v repeats v):
  //   f8010113 112223 212423 312623 412823 512a23 612c23 712e23 2812023 2912223 2a12423 2b12623 2c12823
  //   2d12a23 2e12c23 2f12e23 5012023 5112223 5212423 5312623 5412823 5512a23 5612c23 5712e23 7812023
  //   7912223 7a12423 7b12623 7c12823 7d12a23 7e12c23 7f12e23 341022f3 512023 10513 342025f3 cc000ef 12283
  //   34129073 7c12f83 7812f03 7412e83 7012e03 6c12d83 6812d03 6412c83 6012c03 5c12b83 5812b03 5412a83
  //   5012a03 4c12983 4812903 4412883 4012803 3c12783 3812703 3412683 3012603 2c12583 2812503 2412483
  //   2012403 1c12383 1812303 1412283 1012203 c12183 812103 412083 8010113 30200073 100513 50593 73 8067
  //   c00087b7 a7a023 8067 2852703 100793 f70463 8067 2c52703 c00087b7 e7a023 8067 b00793 2f58463 800007b7
  //   b78793 f59c63 5f5e7b7 c0008737 ff78793 f72023 8067 8067 2852703 100793 f71863 2c52703 c00087b7
  //   e7a023 52783 478793 f52023 8067 100613 100513 60593 73 100513 60593 73 100713 200793 100513 78593 73
  //   f706b3 e6b5b3 78713 fc0594e3 68793 100513 78593 73 f706b3 e6b5b3 78713 fa0594e3 fe1ff06f 65339*0
  //   8004117 10010113 fffc0297 f828293 30529073 fffc0297 29c28293 34129073 12b7 80028293 3042a073 8000293
  //   3002a073 30046073 30200073
endmodule

module ProgramCounter (
  input  PCE,
  input  CLK,
  input  JMP,
  input  [31:0] ADDR,
  output EALIGN,
  output [31:0] PC
);

  wire or_1_out;

  and and_1 (EALIGN, or_1_out, JMP);
  or or_1 (or_1_out, ADDR[0], ADDR[1]);
  Counter #(.max('h3fffffff), .width(30)) counter_1 (
    .load(JMP), .count(PCE), .clk(CLK), .D(ADDR[31:2]), .Q(PC[31:2]));  // open: clr, up, carry
  Register #(.trigger("high"), .width(32)) register_1 (.D({PC[31:2], 2'b00}), .clk(1'b1));  // open: en, Q, clr

  assign PC[1:0] = 2'b00;
endmodule

module ArithmeticLogicUnit (
  input  [31:0] A,
  input  [31:0] PC,
  input  PCREL,
  input  [31:0] B,
  input  [4:0] SEL,
  input  [31:0] IMM,
  input  OPIMM,
  input  CLK,
  output [31:0] R,
  output RDY,
  output EQ,
  output LT,
  output LTU
);

  wire comparator_3_lt, comparator_4_lt, decoder_1_out0, decoder_1_out1, decoder_1_out2, decoder_1_out3,
       decoder_1_out4, decoder_1_out5, decoder_1_out6, decoder_1_out7, decoder_1_out8, decoder_1_out9,
       decoder_1_out10, decoder_1_out11, decoder_1_out12, decoder_1_out13, decoder_1_out14, decoder_1_out15,
       decoder_1_out16, decoder_1_out21, OVF;
  wire [31:0] ANDV, DIFF, multiplier_1_out, ORV, PROD, PRODH, PRODHSU, PRODHU, QUOT, QUOTU, REMS, REMU, SARV,
       shifter_1_out, shifter_2_out, shifter_3_out, SHLV, SHRV, SLTUV, SLTV, SUM, X, XORV, Y;
  wire [32:0] bit_extender_1_out, bit_extender_2_out;
  wire [32:31] multiplier_1_cout;

  assign bit_extender_1_out = {{1{X[31]}}, X};  // Bit_Extender bit_extender_1
  assign bit_extender_2_out = {{1{1'b0}}, Y};  // Bit_Extender bit_extender_2
  Multiplier #(.mode("twosComplement"), .width(33)) multiplier_1 (
    .a(bit_extender_1_out), .b(bit_extender_2_out), .out({PRODHSU[0], multiplier_1_out}),
    .cout({multiplier_1_cout, PRODHSU[31:1]}));  // open: cin
  Adder #(.width(32)) adder_1 (.a(X), .b(Y), .out(SUM));  // open: cin, cout
  Subtractor #(.width(32)) subtractor_1 (.a(X), .b(Y), .out(DIFF));  // open: bin, bout
  Multiplier #(.mode("twosComplement"), .width(32)) multiplier_2 (.a(X), .b(Y), .out(PROD), .cout(PRODH));  // open: cin
  Multiplier #(.width(32)) multiplier_3 (.a(X), .b(Y), .cout(PRODHU));  // open: out, cin
  Divider #(.mode("twosComplement"), .width(32)) divider_1 (.a(X), .b(Y), .out(QUOT), .rem(REMS));  // open: upper
  Divider #(.width(32)) divider_2 (.a(X), .b(Y), .out(QUOTU), .rem(REMU));  // open: upper
  LED F_EQ (.in(EQ));
  Comparator #(.width(32)) comparator_1 (.a(A), .b(B), .eq(EQ), .lt(LT));  // open: gt
  Comparator #(.mode("unsigned"), .width(32)) comparator_2 (.a(A), .b(B), .lt(LTU));  // open: gt, eq
  LED F_LT (.in(LT));
  Register #(.trigger("high"), .width(32)) u_SUM (.D(SUM), .clk(1'b1));  // open: en, Q, clr
  Register #(.trigger("high"), .width(32)) u_DIFF (.D(DIFF), .clk(1'b1));  // open: en, Q, clr
  Register #(.trigger("high"), .width(32)) u_PROD (.D(PROD), .clk(1'b1));  // open: en, Q, clr
  Register #(.trigger("high"), .width(32)) u_PRODH (.D(PRODH), .clk(1'b1));  // open: en, Q, clr
  Register #(.trigger("high"), .width(32)) u_PRODHU (.D(PRODHU), .clk(1'b1));  // open: en, Q, clr
  Register #(.trigger("high"), .width(32)) u_PRODHSU (.D(PRODHSU), .clk(1'b1));  // open: en, Q, clr
  Register #(.trigger("high"), .width(32)) u_QUOT (.D(QUOT), .clk(1'b1));  // open: en, Q, clr
  Register #(.trigger("high"), .width(32)) u_REMS (.D(REMS), .clk(1'b1));  // open: en, Q, clr
  Register #(.trigger("high"), .width(32)) u_QUOTU (.D(QUOTU), .clk(1'b1));  // open: en, Q, clr
  Register #(.trigger("high"), .width(32)) u_REMU (.D(REMU), .clk(1'b1));  // open: en, Q, clr
  LED F_LTU (.in(LTU));
  assign ORV = X | Y;  // OR_Gate or_1, 32 bits wide
  assign ANDV = X & Y;  // AND_Gate and_1, 32 bits wide
  assign XORV = X ^ Y;  // XOR_Gate xor_1, 32 bits wide
  Shifter #(.width(32)) shifter_1 (.in(X), .\dist (Y[4:0]), .out(shifter_1_out));
  Shifter #(.shift("lr"), .width(32)) shifter_2 (.in(X), .\dist (Y[4:0]), .out(shifter_2_out));
  Shifter #(.shift("ar"), .width(32)) shifter_3 (.in(X), .\dist (Y[4:0]), .out(shifter_3_out));
  Comparator #(.width(32)) comparator_3 (.a(X), .b(Y), .lt(comparator_3_lt));  // open: gt, eq
  Comparator #(.mode("unsigned"), .width(32)) comparator_4 (.a(X), .b(Y), .lt(comparator_4_lt));  // open: gt, eq
  Multiplexer #(.width(32)) multiplexer_1 (.in0(shifter_1_out), .in1({32{1'b0}}), .out(SHLV), .sel(OVF));
  Multiplexer #(.width(32)) multiplexer_2 (.in0(shifter_2_out), .in1({32{1'b0}}), .out(SHRV), .sel(OVF));
  Multiplexer #(.width(32)) multiplexer_3 (.in0(shifter_3_out), .in1({32{1'b0}}), .out(SARV), .sel(OVF));
  assign SLTV = {{31{1'b0}}, comparator_3_lt};  // Bit_Extender bit_extender_3
  assign SLTUV = {{31{1'b0}}, comparator_4_lt};  // Bit_Extender bit_extender_4
  Register #(.trigger("high"), .width(32)) u_ORV (.D(ORV), .clk(1'b1));  // open: en, Q, clr
  Register #(.trigger("high"), .width(32)) u_ANDV (.D(ANDV), .clk(1'b1));  // open: en, Q, clr
  Register #(.trigger("high"), .width(32)) u_XORV (.D(XORV), .clk(1'b1));  // open: en, Q, clr
  Register #(.trigger("high"), .width(32)) u_SHLV (.D(SHLV), .clk(1'b1));  // open: en, Q, clr
  Register #(.trigger("high"), .width(32)) u_SHRV (.D(SHRV), .clk(1'b1));  // open: en, Q, clr
  Register #(.trigger("high"), .width(32)) u_SARV (.D(SARV), .clk(1'b1));  // open: en, Q, clr
  Register #(.trigger("high"), .width(32)) u_SLTV (.D(SLTV), .clk(1'b1));  // open: en, Q, clr
  Register #(.trigger("high"), .width(32)) u_SLTUV (.D(SLTUV), .clk(1'b1));  // open: en, Q, clr
  LED F_SUM (.in(decoder_1_out0));
  LED F_SHLV (.in(decoder_1_out1));
  LED F_SLTV (.in(decoder_1_out2));
  LED F_SLTUV (.in(decoder_1_out3));
  LED F_XORV (.in(decoder_1_out4));
  LED F_SHRV (.in(decoder_1_out5));
  LED F_ORV (.in(decoder_1_out6));
  LED F_ANDV (.in(decoder_1_out7));
  LED F_PROD (.in(decoder_1_out8));
  LED F_PRODH (.in(decoder_1_out9));
  LED F_PRODHSU (.in(decoder_1_out10));
  LED F_PRODHU (.in(decoder_1_out11));
  LED F_QUOT (.in(decoder_1_out12));
  LED F_QUOTU (.in(decoder_1_out13));
  LED F_REMS (.in(decoder_1_out14));
  LED F_REMU (.in(decoder_1_out15));
  LED F_DIFF (.in(decoder_1_out16));
  LED F_SARV (.in(decoder_1_out21));
  Decoder #(.enable("false"), .select(5)) decoder_1 (
    .out0(decoder_1_out0), .out1(decoder_1_out1), .out2(decoder_1_out2), .out3(decoder_1_out3),
    .out4(decoder_1_out4), .out5(decoder_1_out5), .out6(decoder_1_out6), .out7(decoder_1_out7),
    .out8(decoder_1_out8), .out9(decoder_1_out9), .out10(decoder_1_out10), .out11(decoder_1_out11),
    .out12(decoder_1_out12), .out13(decoder_1_out13), .out14(decoder_1_out14), .out15(decoder_1_out15),
    .out16(decoder_1_out16), .out21(decoder_1_out21), .sel(SEL));  // open: out17, out18, out19, out20, out22, out23, out24, out25, out26, out27, out28, out29, out30, out31
  Multiplexer #(.select(5), .width(32)) multiplexer_4 (
    .in0(SUM), .in1(SHLV), .in2(SLTV), .in3(SLTUV), .in4(XORV), .in5(SHRV), .in6(ORV), .in7(ANDV),
    .in8(PROD), .in9(PRODH), .in10(PRODHSU), .in11(PRODHU), .in12(QUOT), .in13(QUOTU), .in14(REMS),
    .in15(REMU), .in16(DIFF), .in17({32{1'b0}}), .in18({32{1'b0}}), .in19({32{1'b0}}), .in20({32{1'b0}}),
    .in21(SARV), .in22({32{1'b0}}), .in23({32{1'b0}}), .in24({32{1'b0}}), .in25({32{1'b0}}),
    .in26({32{1'b0}}), .in27({32{1'b0}}), .in28({32{1'b0}}), .in29({32{1'b0}}), .in30({32{1'b0}}),
    .in31({32{1'b0}}), .out(R), .sel(SEL));
  Register #(.trigger("high"), .width(32)) VR (.D(R), .clk(1'b1));  // open: en, Q, clr
  or or_2 (OVF, Y[5], Y[6], Y[7], Y[8], Y[9], Y[10], Y[11], Y[12], Y[13], Y[14], Y[15], Y[16], Y[17], Y[18], Y[19], Y[20], Y[21], Y[22], Y[23], Y[24], Y[25], Y[26], Y[27], Y[28], Y[29], Y[30], Y[31]);
  Register #(.trigger("high"), .width(32)) VX (.D(X), .clk(1'b1));  // open: en, Q, clr
  Multiplexer #(.width(32)) multiplexer_5 (.in0(A), .in1(PC), .out(X), .sel(PCREL));
  LED #(.active("false")) X_A (.in(PCREL));
  LED X_PC (.in(PCREL));
  Register #(.trigger("high"), .width(32)) VY (.D(Y), .clk(1'b1));  // open: en, Q, clr
  Multiplexer #(.width(32)) multiplexer_6 (.in0(B), .in1(IMM), .out(Y), .sel(OPIMM));
  LED #(.active("false")) Y_B (.in(OPIMM));
  LED Y_IMM (.in(OPIMM));
  LED F_READY (.in(1'b1));

  assign RDY = 1'b1;

  // Other names for the same wires on the sheet: VX[31:0] = A; VY[31:0] = B; Y4_0[4:0] = Y[4:0]
endmodule

module MaskingUnit (
  input  M0,
  input  M1,
  input  M2,
  input  [31:0] DI,
  input  M3,
  output [31:0] DO
);

  wire [7:0] bit_extender_1_out, bit_extender_2_out, bit_extender_3_out, bit_extender_4_out;

  assign DO[7:0] = DI[7:0] & bit_extender_1_out;  // AND_Gate and_1, 8 bits wide
  assign bit_extender_1_out = {{7{M0}}, M0};  // Bit_Extender bit_extender_1
  assign DO[15:8] = DI[15:8] & bit_extender_2_out;  // AND_Gate and_2, 8 bits wide
  assign bit_extender_2_out = {{7{M1}}, M1};  // Bit_Extender bit_extender_2
  assign DO[23:16] = DI[23:16] & bit_extender_3_out;  // AND_Gate and_3, 8 bits wide
  assign bit_extender_3_out = {{7{M2}}, M2};  // Bit_Extender bit_extender_3
  assign DO[31:24] = DI[31:24] & bit_extender_4_out;  // AND_Gate and_4, 8 bits wide
  assign bit_extender_4_out = {{7{M3}}, M3};  // Bit_Extender bit_extender_4
endmodule

module LeftShifter (
  input  A0,
  input  A1,
  input  [31:0] DI,
  output [31:0] DO
);

  wire [31:0] multiplexer_1_out, shifter_1_out, shifter_2_out;

  Shifter #(.width(32)) shifter_1 (.in(DI), .\dist (5'b01000), .out(shifter_1_out));
  Multiplexer #(.width(32)) multiplexer_1 (.in0(DI), .in1(shifter_1_out), .out(multiplexer_1_out), .sel(A0));
  Multiplexer #(.width(32)) multiplexer_2 (.in0(multiplexer_1_out), .in1(shifter_2_out), .out(DO), .sel(A1));
  Shifter #(.width(32)) shifter_2 (.in(multiplexer_1_out), .\dist (5'b10000), .out(shifter_2_out));
endmodule

module RightShifter (
  input  A0,
  input  A1,
  input  [31:0] DI,
  output [31:0] DO
);

  wire [31:0] multiplexer_1_out, shifter_1_out, shifter_2_out;

  Shifter #(.shift("lr"), .width(32)) shifter_1 (.in(DI), .\dist (5'b01000), .out(shifter_1_out));
  Multiplexer #(.width(32)) multiplexer_1 (.in0(DI), .in1(shifter_1_out), .out(multiplexer_1_out), .sel(A0));
  Multiplexer #(.width(32)) multiplexer_2 (.in0(multiplexer_1_out), .in1(shifter_2_out), .out(DO), .sel(A1));
  Shifter #(.shift("lr"), .width(32)) shifter_2 (.in(multiplexer_1_out), .\dist (5'b10000), .out(shifter_2_out));
endmodule

module SignExtender (
  input  [31:0] DI,
  input  LB,
  input  LDSX,
  output [31:0] DO
);

  wire and_1_out;
  wire [6:0] bit_extender_1_out;
  wire [15:0] bit_extender_2_out;

  and and_1 (and_1_out, LB, LDSX);
  Multiplexer multiplexer_1 (.in0(DI[15]), .in1(DI[7]), .out(DO[15]), .sel(and_1_out));
  Multiplexer #(.width(7)) multiplexer_2 (.in0(DI[14:8]), .in1(bit_extender_1_out), .out(DO[14:8]), .sel(and_1_out));
  assign bit_extender_1_out = {{6{DI[7]}}, DI[7]};  // Bit_Extender bit_extender_1
  Multiplexer #(.width(16)) multiplexer_3 (.in0(DI[31:16]), .in1(bit_extender_2_out), .out(DO[31:16]), .sel(LDSX));
  assign bit_extender_2_out = {{15{DO[15]}}, DO[15]};  // Bit_Extender bit_extender_2

  assign DO[7:0] = DI[7:0];
endmodule

module BusInterface (
  input  [31:0] DI,
  input  [31:0] DOUT,
  input  RST,
  input  CLK,
  input  LDSX,
  input  LOAD0,
  input  LOAD1,
  input  STORE0,
  input  STORE1,
  input  [31:0] ADDR,
  output [31:0] DIN,
  output [31:0] DO,
  output STROBE,
  output EALIGN,
  output BM0,
  output BM1,
  output BM2,
  output BM3,
  output nRW,
  output [29:0] A
);

  wire LB, LD, not_1_out;
  wire [31:0] bit_extender_1_out, leftshifter_1_do, maskingunit_1_do, maskingunit_2_do, rightshifter_1_do,
       signextender_1_do;

  MaskingUnit maskingunit_1 (.DO(maskingunit_1_do), .DI(DI), .M0(BM0), .M1(BM1), .M2(BM2), .M3(BM3));
  LeftShifter leftshifter_1 (.DO(leftshifter_1_do), .DI(DOUT), .A0(ADDR[0]), .A1(ADDR[1]));
  MaskingUnit maskingunit_2 (.DO(maskingunit_2_do), .DI(leftshifter_1_do), .M0(BM0), .M1(BM1), .M2(BM2), .M3(BM3));
  not not_1 (not_1_out, RST);
  // PlaRom #(.Contents("0*4 1 2 0*5 2 0*4 2 0*4 2 0*4 2 0*3 1 1 0 0 2 2 1 1 2 0 0 2 1 1 0 2 2 0 1 1 2 2 0 0 2 2 1 0 1 2*3 1 2 1 0 2 1 0 1 2 1 2 1 2 1 0 1 2 1 1 0 1 2 2 1 1 2 1 0 1 1 0 0 2 0 1 1 2 0*3 1 2 1 0 1 2 1 2 1 2 1 0 1 1 0*3 2 1 1 0 2 0*3 2 0 0 2 0 0 2 2 0*3 2 0*3 2*3 0 2 0 0 2 2 0 0 2 2 0 2 0 2 2 0 0 1 0*8 1 0*7 1 0*8 1 0*7 1 0*8 1 1 0*6 1 1 0*6 1 1 0*6 1 1 0*6 1 0*7 1 0*7 1 1 0*6 1 1 0*7 1 0*7 1 0*8 1 1 0*6 1 1 0*6 1 0*7 1 0*8 1 0*7 1 0*8 1 0*7 1 0*7 1 0*7 1 0*7 1 0*7 1"), .\and (27), .outputs(8)) MaskGen: pin names not known; wires that end beside it: {ADDR[1:0], STORE1, STORE0, LOAD1, LOAD0}, {LB, LD, nRW, BM3, BM2, BM1, BM0, EALIGN}
  Register #(.trigger("high"), .width(32)) MAR (.D(ADDR), .clk(1'b1));  // open: en, Q, clr
  RightShifter rightshifter_1 (.DO(rightshifter_1_do), .DI(maskingunit_1_do), .A0(ADDR[0]), .A1(ADDR[1]));
  and and_1 (STROBE, not_1_out, CLK);
  SignExtender signextender_1 (.DO(signextender_1_do), .DI(rightshifter_1_do), .LB(LB), .LDSX(LDSX));
  Register #(.trigger("high"), .width(32)) MDO (.D(maskingunit_2_do), .clk(nRW));  // open: en, Q, clr
  assign DO = nRW ? maskingunit_2_do : 32'bz;  // Controlled_Buffer controlled_buffer_1
  assign bit_extender_1_out = {{31{LD}}, LD};  // Bit_Extender bit_extender_1
  assign DIN = bit_extender_1_out & signextender_1_do;  // AND_Gate and_2, 32 bits wide
  Register #(.trigger("high"), .width(32)) MDI (.D(DIN), .clk(1'b1));  // open: en, Q, clr

  assign A = ADDR[31:2];

  // Other names for the same wires on the sheet: A0 = ADDR[0]; A1 = ADDR[1]; M0 = BM0; M1 = BM1; M2 = BM2; M3 = BM3;
  //   ST = nRW; SX = LDSX

  // Notes on the sheet:
  //   RST: pull=up
endmodule

module FetchUnit (
  input  IRQ,
  input  HOLD,
  input  [31:0] DIN,
  input  SX,
  input  [31:0] EMA,
  input  LD0,
  input  [31:0] PC_IN,
  input  LD1,
  input  ST0,
  input  ST1,
  input  CLK,
  output [31:0] INSTR,
  output PCE,
  output LDSX,
  output LOAD0,
  output [31:0] ADDR,
  output LOAD,
  output LOAD1,
  output [31:0] PC,
  output STORE0,
  output STORE1,
  output GRANT
);

  wire ILD, IRG, IRQ_t, not_1_out, not_2_out, or_2_out, PCM;
  wire [31:0] multiplexer_3_out;

  or or_1 (PCM, or_2_out, LOAD);
  or or_2 (or_2_out, ST1, ST0);
  and and_1 (IRQ_t, IRQ, not_1_out);
  not not_1 (not_1_out, HOLD);
  nor nor_1 (PCE, PCM, HOLD, IRQ_t);
  or or_3 (LOAD, LD1, LD0);
  or or_4 (ILD, IRQ_t, PCE);
  LED FETCHING (.in(PCE));
  and and_2 (LDSX, LOAD, SX);
  Multiplexer multiplexer_1 (.in0(PCE), .in1(LD0), .out(LOAD0), .sel(LOAD));
  Multiplexer multiplexer_2 (.in0(PCE), .in1(LD1), .out(LOAD1), .sel(LOAD));
  Register #(.width(32)) INS (.D(multiplexer_3_out), .en(ILD), .clk(CLK), .Q(INSTR));  // open: clr
  Multiplexer #(.width(32)) multiplexer_3 (.in0(DIN), .in1(32'h13), .out(multiplexer_3_out), .sel(IRG));
  Register #(.width(32)) PCR (.D(PC_IN), .en(ILD), .clk(CLK), .Q(PC));  // open: clr
  not not_2 (not_2_out, PCM);
  Multiplexer #(.width(32)) multiplexer_4 (.in0(EMA), .in1(PC_IN), .out(ADDR), .sel(not_2_out));
  D_Flip_Flop d_ff_1 (.D(IRQ_t), .clk(CLK), .Q(GRANT));  // open: Qn, preset, reset
  or or_5 (IRG, IRQ_t, GRANT);

  assign STORE0 = ST0;
  assign STORE1 = ST1;
endmodule

module InstructionDecoder (
  input  EQ,
  input  LT,
  input  RDY,
  input  LTU,
  input  CLK,
  input  RST,
  input  [31:0] INSTR,
  output [4:0] RD,
  output [4:0] RS1,
  output [4:0] RS2,
  output OPIMM,
  output [11:0] CSRI,
  output HOLD,
  output BRANCH,
  output CSR_EN,
  output PCREL,
  output LINK,
  output ILL,
  output SX,
  output WFI,
  output LD0,
  output RET,
  output LD1,
  output BRK,
  output ST0,
  output SYS,
  output ST1,
  output CSR_SEL,
  output [4:0] ALU_OP,
  output CSR_BIT,
  output CSR_CLR,
  output [31:0] IMM,
  output [31:0] CSR_IMM
);

  wire BRANCH_t, CTR, FUNCT, HOLD_t, IM0, IM1, nand_1_out, not_1_out, OPIMM_t, PCREL_t, RD_t, RS1_t, RS2_t,
       S0, S4_1_0, S4_1_1, S10_5, S19_12, S30_20, SEL, SYS_t, VLD_AL, VLD_BL, VLD_CS;
  wire [3:0] and_9_out, and_10_out;
  wire [7:1] CLF_p2;
  wire [11:0] bit_extender_1_out;
  wire [18:0] bit_extender_2_out;

  Register #(.trigger("high"), .width(32)) V_INS (.D(INSTR), .clk(1'b1));  // open: en, Q, clr
  // PlaRom #(.Contents("0*3 2 2 1 2 2 0*6 1 0 2 1 2 0*6 2 2 1*3 0*6 1 2 1*3 0*6 2 2 1 1 2 0*6 2*3 1 1 0*6 1 1 0 1 1 0*6 1*3 2 2 0*6 1 2 2 1 1 0*3 1 0 1 2 2 1*3 0 0 2 1 0 2*3 1*3 0 0 1 2 2 1 2 2 1*3 2 0 0 2*5 1*4 0 0 2 1 1 2 2 1*3 0 2 0 2 1 2*3 1*3 0 1 0*8 2 0*9 2 0*9 2 0*9 1 0*9 1 0*7 1 0 1 0*7 2 1 0 2 0*7 1 2 2 1 0*5 2 0 0 2*3 0*5 1 0 0 2 1 1 0*6 2 0 2 1 2 0*6 1 0 1 0*8 1 0*8 1 0*8 1 0*8 1 0*7 1 0*7 1 0*7 1 0*8 1 0*8 1 0*7 1 0*7 1 0*7 1 0*7 1 0*7 1 0*8 1 0*7 1 0*7 1 0*7 1 0*7 1 0*7 1 0*7 1 0*7 1 0*7 1 0*7 1 0*7 1"), .\and (26), .outputs(8)) CLF: pin names not known; wires that end beside it: {INSTR[14:12], INSTR[6:2], LTU, LT, EQ}, {CLF_p2, SEL}
  // PlaRom #(.Contents("0*4 2 2 1 2*4 1 0*3 1 0 2 1 2*3 0 2 0 0 2 2 1*3 2 2 0 1 1 0 0 2 1*3 2 2 0 1 0 1 1 0 1*3 2 2 0 0 1 0 1*5 2 2 0 1*3 2 2 1 1 0 2 2 1*3 2 1 2 1*3 2 2 1 1 2 1 1 2 1*3 2 2 1 1 0 1 1 2 1*3 2 2 1 0 1 2 1*5 2 2 1 1 2 1*6 2 2 1 0 1*7 2 2 1 1 0 1*6 2 2 1*3 0 1*5 2 2 1 0*3 2 2 1 2*4 1*4 2 2 1 0 2*3 1 2 0 0 2 2 1*3 2 2 1 0 1 0 2 2 1*3 2 2 1*4 2 2 1 1 0 2 2 1 0*3 1 1 2 1 2*3 1 0*8 1 0*8 1 0*8 1 0*8 1 0*8 1 0*8 1 0*9 1 0*8 1 0*9 1 0*9 1 0*8 1 0*9 1 0*8 1 0*9 1 0*9 1*3 0*6 1 0*9 1 1 0*7 1 1 0*7 1 0*9 1"), .\and (21), .outputs(9)) DEC_BL: pin names not known; wires that end beside it: {CTR, INSTR[14:12], INSTR[6:0]}, {VLD_BL, ST1, ST0, LD1, LD0, SX, LINK, BRANCH_t, PCREL_t}
  // PlaRom #(.Contents("2 0*3 1 2 2 1 1 2 2 0 1 0 0 2 0 1 1 2 1 1 2 2 1 0*4 1*3 2 1 1 2 2 1 0 1 0*3 1 0 2 1 1 2 2 1*3 2 1 2 1 0 2 1 1 2 2 1 0 1*5 0 2 1 1 2 2 1 0*5 1 2 2 1 1 2 2 1*3 0 1 2 1 0 2 1 1 2 2 1*7 2 2 1 1 2 2 1 0 1 2 1 2 1 0 2 1 1 2 2 1 2 1*5 2 2 1 1 2 2 1 2*3 0 0 1 2 2 1 1 2 2 0 1 0 2 2 0 1 1 2 1 1 2 2 1 0 0 2 0 1*3 2 1 1 2 2 1 0 1 2 0 0 1 0 2 1 1 2 2 1 1 0 0 2 0 1 0 2 1 1 2 2 1 1 2 0 2 0 1 2 2 1 1 2 2 0 1 2 0 0 2 1 2 2 1 1 2 2 0 1 0 0 2 2 1 1 2 1 1 2 2 1 0 1 0 0 2 1 0 2 1 1 2 2 1 1 1 1 0 1 0*3 1 0*4 1 0 1 0*6 1 0*6 1 1 0 0 1 0 1 1 0*7 1 0*6 1 0*6 1 0*7 1 0*6 1 0*8 1 0*6 1 0*6 1 0*6 1 0*7 1 0*6 1 0*7 1 0*6 1 0*6 1"), .\and (20), .outputs(7)) DEC_AL: pin names not known; wires that end beside it: {INSTR[25], INSTR[14:12], INSTR[6:0], CTR, INSTR[30]}, {VLD_AL, FUNCT, ALU_OP}
  assign RD = {5{RD_t}} & INSTR[11:7];  // AND_Gate and_1, 5 bits wide
  LED COND (.in(CLF_p2[1]));
  LED R (.in(CLF_p2[2]));
  LED I (.in(CLF_p2[3]));
  LED S (.in(CLF_p2[4]));
  LED B (.in(CLF_p2[5]));
  Register #(.trigger("high"), .width(5)) V_RD (.D(RD), .clk(1'b1));  // open: en, Q, clr
  LED U (.in(CLF_p2[6]));
  LED J (.in(CLF_p2[7]));
  assign RS1 = {5{RS1_t}} & INSTR[19:15];  // AND_Gate and_2, 5 bits wide
  nand nand_1 (nand_1_out, CTR, RDY);
  and and_3 (HOLD, HOLD_t, nand_1_out, SEL);
  // PlaRom #(.Contents("0*4 2 2 1 2*4 1 0 0 2 0 0 2 2 1*3 2 2 1 0 0 1 1 0 0 2 1*3 2 2 1 0 0 1 0 1 1 0 1*3 2 2 1 0*3 1 0 1*5 2 2 1 0 0 1*3 2 2 1 1 0 2 2 1 0 0 1*3 2*3 1 1 2 2 0 1 0*4 1 0 2 1 2*3 1 0*3 2 0 1 1 2 1 0 2 2 1 0*4 1*3 2 1 0 2 2 1 0 1 2 0 0 1 1 2 1 0 2 2 1 0 1 0*3 1 1 2 1 0 2 2 1 1 0*4 1 2 2 1 1 2 2 1 1 0 1 0 1 1 2 1*3 2 2 1 0 1 2 1 2 1 2 2 1 1 2 2 1 0 1*5 2 0 1 1 2 2 1 0*3 2 0 1 1 2 1 1 2 2 1 0 0 1 2 0 2*3 1 1 2 2 1 0 1 0*3 1 0 2 1 1 2 2 1 1 0 1 1 2*3 0 1 1 2 2 1 0*3 1*4 0 1 1 2 2 1 0 0 1 1 0 1*3 2*4 1 0 1 2 1 2 1 0 2 1 1 2 2 1 0 1*5 0 0 1 1 2 2 1 0*5 1 2 2 1 0 2 2 1 1 0*3 2*4 1 1 2 2 1 0*3 2 0 2*3 1 1 2 2 1 0 1 0*3 1 0 2 1 0 2 2 1*3 2 1 2 1 0 2 1 0 2 2 1 0 0 1*3 2 2 1 0 2*3 1 0 0 1 0 1*3 0 1 1 2 2 1 0 1*5 0 2 1 0 2 2 1 0 1 1 0 0 1*5 0 1*4 0 1 1 0 1 0 1 1 0 1*4 0 1 0 1 0*5 1 0 0 1 0 1 0 0 1 0 1 0 0 1 0 1 0*4 1 0*5 1 1 0*3 1 0*4 1 0*4 1 0*5 1 0*4 1 0*4 1 0*4 1 0*4 1 0*4 1 1 0*3 1 0*4 1 0*5 1 0*4 1 0*4 1 0*4 1 0*4 1 0*4 1 0*4 1 0*4 1"), .\and (32), .outputs(5)) DEC_CR: pin names not known; wires that end beside it: {INSTR[25], INSTR[14:12], INSTR[6:0], CTR, INSTR[30]}, {HOLD_t, OPIMM_t, RS2_t, RS1_t, RD_t}
  // PlaRom #(.Contents("1 0 0 2*4 1 1 2 2 1 0 2 0 2*3 1 1 2 2 0 1*3 2*3 1 1 2 2 1*3 0 1*3 2*4 1 0 2*5 1 1 2 2 1 2 0 2*4 1 1 2 2 1 2 2 0 2*3 1 1 2 2 1 0*4 1 1 0 0 1 0 1*3 0*4 1 0*7 1 0*7 1 0*5 1 0"), .\and (7), .outputs(6)) DEC_CS: pin names not known; wires that end beside it: {CTR, INSTR[14:12], INSTR[6:0]}, {VLD_CS, SYS_t, CSR_CLR, CSR_BIT, CSR_SEL, CSR_EN}
  Register #(.trigger("high"), .width(5)) V_RS1 (.D(RS1), .clk(1'b1));  // open: en, Q, clr
  D_Flip_Flop d_ff_1 (.D(HOLD), .clk(CLK), .Q(CTR), .Qn(S0), .reset(RST));  // open: preset
  LED S1 (.in(CTR));
  LED u_S0 (.in(S0));
  assign RS2 = {5{RS2_t}} & INSTR[24:20];  // AND_Gate and_4, 5 bits wide
  Register #(.trigger("high"), .width(5)) V_RS2 (.D(RS2), .clk(1'b1));  // open: en, Q, clr
  and and_5 (OPIMM, OPIMM_t, SEL);
  and and_6 (BRANCH, BRANCH_t, SEL);
  and and_7 (PCREL, PCREL_t, SEL);
  // PlaRom #(.Contents("0*10 2 2 0*5 2 0*7 2 1*3 0*13 2 2 1*5 0*6 2 2 1*4 2 0*6 2*4 1 2 1 0*7 2 1 2 2 1 2 0*7 2 0*3 2 2 0*7 2 0 1 0 2 0*8 2 0 0 2 0 1 0*7 2 0 1 2 0*9 2 2 0 0 1 0*8 2 1 2 1 0*5 1 0*4 1 0*4 1 0*4 1 0*5 1 0*5 1 0*5 1 0*5 1 0*4 1 0*4 1 0*4 1 0*4 1 0*4 1"), .\and (13), .outputs(5)) SYSDEC: pin names not known; wires that end beside it: {VLD_CS, VLD_AL, VLD_BL, S0, SYS_t, INSTR[29:28], INSTR[22:20], FUNCT, IM1, IM0}, {SYS, BRK, RET, WFI, ILL}
  // PlaRom #(.Contents("0*5 1 0 2 1 2 0*5 2 2 1 2 2 0 2 0*3 2 2 1 2*3 0*4 2 2 1 1 2 2 0*4 2*3 1 1 2 0*4 1 0 1*3 2 0*4 1 1 0 1 1 2 0*4 1*3 2 2 0*4 2*3 1*3 0*5 2 2 1 0 2 0*5 2 2 0 1 1 0*5 1 0 1*3 0*5 1*3 2 2 0 0 2 0 0 1 1 0 1 1 0*3 1 0 1 1 0 1 1 0*6 2 1*3 0*5 2*3 1 1 0*5 1 1 0 1 1 0 2 0*3 2 2 1 1 2 0 2 0*3 2*3 1 1 0 2 0*3 1 1 0 1 1 0 2 0*3 1*3 2 2 0*4 2 1 2 1*3 1 1 0*6 1 0*7 1 0*6 1 0*6 1 0*6 1 0*6 1 0*6 1 0*6 1 0*7 1 0 1 0*4 1 0*6 1 0*6 1 0 1 0*4 1 0*6 1 0*7 1 0*7 1 0*6 1 0*7 1 0*6 1 0*6 1 0*6 1 0*6 1"), .\and (23), .outputs(7)) IMMDEC: pin names not known; wires that end beside it: {INSTR[31], INSTR[20], INSTR[13:12], INSTR[7:2]}, {S30_20, S19_12, IMM[11], S10_5, S4_1_1, S4_1_0, IMM[0]}
  assign CSRI = INSTR[31:20] & bit_extender_1_out;  // AND_Gate and_8, 12 bits wide
  assign bit_extender_1_out = {{11{CSR_EN}}, CSR_EN};  // Bit_Extender bit_extender_1
  assign and_9_out = {4{S4_1_1}} & INSTR[11:8];  // AND_Gate and_9, 4 bits wide
  assign and_10_out = INSTR[24:21] & {4{S4_1_0}};  // AND_Gate and_10, 4 bits wide
  not not_1 (not_1_out, S19_12);
  Multiplexer #(.width(8)) multiplexer_1 (
    .in0(INSTR[19:12]), .in1(bit_extender_2_out[7:0]), .out(IMM[19:12]), .sel(not_1_out));
  assign bit_extender_2_out = {{18{INSTR[31]}}, INSTR[31]};  // Bit_Extender bit_extender_2
  Multiplexer #(.width(11)) multiplexer_2 (
    .in0(bit_extender_2_out[18:8]), .in1(INSTR[30:20]), .out(IMM[30:20]), .sel(S30_20));
  Register #(.trigger("high"), .width(12)) V_CSRI (.D(CSRI), .clk(1'b1));  // open: en, Q, clr
  assign IMM[4:1] = and_9_out | and_10_out;  // OR_Gate or_1, 4 bits wide
  assign IMM[10:5] = INSTR[30:25] & {6{S10_5}};  // AND_Gate and_11, 6 bits wide
  Register #(.trigger("high"), .width(32)) V_IMM (.D({INSTR[31], IMM[30:0]}), .clk(1'b1));  // open: en, Q, clr
  assign CSR_IMM = {{27{1'b0}}, INSTR[19:15]};  // Bit_Extender bit_extender_3
  or or_2 (IM0, INSTR[31], INSTR[30], INSTR[25], INSTR[7], INSTR[8], INSTR[9], INSTR[10], INSTR[11], INSTR[15], INSTR[16], INSTR[17], INSTR[18], INSTR[19], INSTR[23], INSTR[24], INSTR[26], INSTR[27]);
  or or_3 (IM1, INSTR[31], INSTR[26], INSTR[27], INSTR[28], INSTR[29]);

  assign IMM[31] = INSTR[31];

  // Other names for the same wires on the sheet: P6_0[6:0] = INSTR[6:0]; CSR = CSR_EN; OP[4:0] = INSTR[6:2];
  //   P7 = INSTR[7]; P11_7[4:0] = INSTR[11:7]; P13_12[1:0] = INSTR[13:12]; P14_12[2:0] = INSTR[14:12];
  //   P19_15[4:0] = INSTR[19:15]; P20 = INSTR[20]; P22_20[2:0] = INSTR[22:20]; P24_20[4:0] = INSTR[24:20];
  //   P24_21[3:0] = INSTR[24:21]; P24_23[1:0] = INSTR[24:23]; P25 = INSTR[25]; P30_25[5:0] = INSTR[30:25];
  //   P27_26[1:0] = INSTR[27:26]; P29_26[3:0] = INSTR[29:26]; P29_28[1:0] = INSTR[29:28]; P30 = INSTR[30];
  //   X0 = IMM[0]; X11 = IMM[11]; P31 = INSTR[31]; P11_8[3:0] = INSTR[11:8]

  // Notes on the sheet:
  //   OP [6:0]
  //   rd/imm [11:7]
  //   funct3/imm [14:12]
  //   rs1/imm [19:15]
  //   rs2/imm [24:20]
  //   funct7/imm [31:25]
endmodule

module ResultMux (
  input  [31:0] ALU,
  input  [31:0] NPC,
  input  [31:0] MDI,
  input  [31:0] CSR,
  input  LINK,
  input  LOAD,
  input  LDCSR,
  output [31:0] RES
);

  wire and_1_out, and_2_out, and_3_out, not_1_out, not_2_out, not_3_out;

  Register #(.trigger("high"), .width(32)) V_ALU (.D(ALU), .clk(1'b1));  // open: en, Q, clr
  Register #(.trigger("high"), .width(32)) V_NPC (.D(NPC), .clk(1'b1));  // open: en, Q, clr
  Register #(.trigger("high"), .width(32)) V_MDI (.D(MDI), .clk(1'b1));  // open: en, Q, clr
  Register #(.trigger("high"), .width(32)) V_CSR (.D(CSR), .clk(1'b1));  // open: en, Q, clr
  assign RES = and_1_out ? ALU : 32'bz;  // Controlled_Buffer controlled_buffer_1
  LED S_ALU (.in(and_1_out));
  LED S_NPC (.in(and_2_out));
  LED S_MDI (.in(and_3_out));
  LED S_CSR (.in(LDCSR));
  and and_1 (and_1_out, not_1_out, not_2_out, not_3_out);
  not not_1 (not_1_out, LINK);
  not not_2 (not_2_out, LOAD);
  not not_3 (not_3_out, LDCSR);
  assign RES = and_2_out ? NPC : 32'bz;  // Controlled_Buffer controlled_buffer_2
  assign RES = and_3_out ? MDI : 32'bz;  // Controlled_Buffer controlled_buffer_3
  and and_2 (and_2_out, LINK, not_2_out, not_3_out);
  and and_3 (and_3_out, LOAD, not_3_out);
  assign RES = LDCSR ? CSR : 32'bz;  // Controlled_Buffer controlled_buffer_4
endmodule

module ControlStatusRegisters (
  input  CLR,
  input  RST,
  input  [31:0] PC,
  input  IRET,
  input  [31:0] CAUSE_IN,
  input  TRAP,
  input  CLK,
  input  OPIMM,
  input  [31:0] RX,
  input  [31:0] IMM,
  input  [11:0] CSR,
  input  BIT,
  input  CSE,
  input  ILL_IN,
  output [31:0] EPC,
  output [31:0] ISR,
  output [31:0] CSR_OUT,
  output EIE,
  output LDCSR,
  output ILL
);

  wire and_5_out, and_8_out, and_9_out, and_10_out, and_11_out, and_12_out, and_13_out, and_14_out,
       and_15_out, and_16_out, and_17_out, comparator_1_eq, decoder_1_out0, decoder_1_out1, decoder_1_out2,
       decoder_1_out3, decoder_1_out4, decoder_1_out6, EPC_t, MIE, not_4_out, not_5_out, not_6_out, or_3_out,
       or_4_out, or_5_out, RES, STR, STW, TMP, VEC, WR;
  wire [1:0] or_2_out;
  wire [4:0] rom_1_data;
  wire [7:3] STX;
  wire [29:0] multiplexer_4_out, or_2_out_2;
  wire [31:0] and_2_out, and_3_out, and_4_out, bit_extender_1_out, bit_extender_2_out, CSRV, IEV,
       multiplexer_2_out, multiplexer_3_out, not_1_out, not_2_out, not_3_out, R_CAUSE_q, R_TEMP_q, STV;

  assign bit_extender_1_out = {{31{BIT}}, BIT};  // Bit_Extender bit_extender_1
  assign bit_extender_2_out = {{31{CLR}}, CLR};  // Bit_Extender bit_extender_2
  LED S_MIE (.in(STV[3]));
  LED S_MPIE (.in(STV[7]));
  or or_1 (STW, IRET, TRAP);
  LED #(.active("false")) F_REG (.in(OPIMM));
  Register #(.trigger("high"), .width(32)) V_IN (.D(CSRV), .clk(1'b1));  // open: en, Q, clr
  assign not_1_out = ~CSRV;  // NOT_Gate not_1, 32 bits wide
  assign not_2_out = ~bit_extender_1_out;  // NOT_Gate not_2, 32 bits wide
  assign not_3_out = ~bit_extender_2_out;  // NOT_Gate not_3, 32 bits wide
  and and_1 (EIE, IEV[11], STV[3]);
  LED F_IMM (.in(OPIMM));
  Multiplexer #(.width(32)) multiplexer_1 (.in0(RX), .in1(IMM), .out(CSRV), .sel(OPIMM));
  Register #(.trigger("high"), .width(12)) V_CSR (.D(CSR), .clk(1'b1));  // open: en, Q, clr
  assign and_2_out = bit_extender_1_out & CSR_OUT & not_1_out;  // AND_Gate and_2, 32 bits wide
  assign and_3_out = CSRV & not_2_out;  // AND_Gate and_3, 32 bits wide
  assign and_4_out = CSRV & not_3_out;  // AND_Gate and_4, 32 bits wide
  Comparator #(.mode("unsigned"), .width(32)) comparator_1 (
    .a(CSRV), .b({32{1'b0}}), .eq(comparator_1_eq));  // open: gt, lt
  and and_5 (and_5_out, comparator_1_eq, BIT);
  assign {or_2_out_2, or_2_out} = and_2_out | and_3_out | and_4_out;  // OR_Gate or_2, 32 bits wide
  not not_4 (not_4_out, and_5_out);
  and and_6 (WR, not_4_out, CSE);
  and and_7 (LDCSR, and_5_out, CSE);
  Multiplexer #(.width(32)) multiplexer_2 (
    .in0({or_2_out_2, or_2_out}), .in1({STV[31:8], STX[7], STV[6:4], STX[3], STV[2:0]}),
    .out(multiplexer_2_out), .sel(STW));
  and and_8 (and_8_out, STR, WR);
  Multiplexer #(.width(32)) multiplexer_3 (.in0({or_2_out_2, or_2_out}), .in1(PC), .out(multiplexer_3_out), .sel(TRAP));
  and and_9 (and_9_out, EPC_t, WR);
  LED F_WR (.in(WR));
  // Probe on multiplexer_2_out
  Register #(.width(32)) R_STATUS (.D(multiplexer_2_out), .en(or_3_out), .clk(CLK), .Q(STV));  // open: clr
  or or_3 (or_3_out, STW, and_8_out);
  Register #(.width(32)) R_IE (.D({or_2_out_2, or_2_out}), .en(and_10_out), .clk(CLK), .Q(IEV));  // open: clr
  and and_10 (and_10_out, MIE, WR);
  Register #(.width(32)) R_TEMP (.D({or_2_out_2, or_2_out}), .en(and_11_out), .clk(CLK), .Q(R_TEMP_q));  // open: clr
  and and_11 (and_11_out, WR, TMP);
  Register #(.width(32)) R_EPC (.D(multiplexer_3_out), .en(or_4_out), .clk(CLK), .Q(EPC));  // open: clr
  or or_4 (or_4_out, TRAP, and_9_out);
  Register #(.width(32)) R_CAUSE (.D(CAUSE_IN), .en(TRAP), .clk(CLK), .Q(R_CAUSE_q));  // open: clr
  ROM #(.addrWidth(13), .dataWidth(5)) rom_1 (.addr({WR, CSR}), .data(rom_1_data));
  assign CSR_OUT = STR ? STV : 32'bz;  // Controlled_Buffer controlled_buffer_1
  assign CSR_OUT = MIE ? IEV : 32'bz;  // Controlled_Buffer controlled_buffer_2
  assign CSR_OUT = TMP ? R_TEMP_q : 32'bz;  // Controlled_Buffer controlled_buffer_3
  assign CSR_OUT = EPC_t ? EPC : 32'bz;  // Controlled_Buffer controlled_buffer_4
  assign CSR_OUT = RES ? R_CAUSE_q : 32'bz;  // Controlled_Buffer controlled_buffer_5
  not not_5 (not_5_out, IRET);
  not not_6 (not_6_out, TRAP);
  Multiplexer #(.width(30)) multiplexer_4 (.in0(or_2_out_2), .in1(30'h3fffffc0), .out(multiplexer_4_out), .sel(RST));
  and and_12 (and_12_out, WR, VEC);
  assign CSR_OUT = decoder_1_out0 ? {32{1'b0}} : 32'bz;  // Controlled_Buffer controlled_buffer_6
  and and_13 (and_13_out, IRET, STV[7]);
  and and_14 (and_14_out, STV[3], not_5_out, not_6_out);
  and and_15 (and_15_out, not_6_out, STV[7]);
  and and_16 (and_16_out, STV[3], TRAP);
  Register #(.width(32)) R_VEC (.D({multiplexer_4_out, 2'b00}), .en(or_5_out), .clk(CLK), .Q(ISR));  // open: clr
  or or_5 (or_5_out, RST, and_12_out);
  assign CSR_OUT = decoder_1_out1 ? 32'h63687a79 : 32'bz;  // Controlled_Buffer controlled_buffer_7
  assign CSR_OUT = decoder_1_out2 ? 32'h1000 : 32'bz;  // Controlled_Buffer controlled_buffer_8
  assign CSR_OUT = decoder_1_out3 ? 32'h1 : 32'bz;  // Controlled_Buffer controlled_buffer_9
  assign CSR_OUT = decoder_1_out4 ? {32{1'b0}} : 32'bz;  // Controlled_Buffer controlled_buffer_10
  Decoder #(.enable("false"), .select(4)) decoder_1 (
    .out0(decoder_1_out0), .out1(decoder_1_out1), .out2(decoder_1_out2), .out3(decoder_1_out3),
    .out4(decoder_1_out4), .out5(STR), .out6(decoder_1_out6), .out7(MIE), .out8(VEC), .out9(TMP),
    .out10(EPC_t), .out11(RES), .sel(rom_1_data[3:0]));  // open: out12, out13, out14, out15
  or or_6 (STX[3], and_13_out, and_14_out);
  or or_7 (STX[7], and_15_out, and_16_out);
  assign CSR_OUT = VEC ? ISR : 32'bz;  // Controlled_Buffer controlled_buffer_11
  assign CSR_OUT = decoder_1_out6 ? 32'h40001100 : 32'bz;  // Controlled_Buffer controlled_buffer_12
  and and_17 (and_17_out, CSE, rom_1_data[4]);
  or or_8 (ILL, and_17_out, ILL_IN);
  LED F_STR (.in(STR));
  LED F_MIE (.in(MIE));
  LED F_VEC (.in(VEC));
  LED F_TMP (.in(TMP));
  LED F_EPC (.in(EPC_t));
  LED F_RES (.in(RES));

  // Other names for the same wires on the sheet: INT = TRAP; PCV[31:0] = EPC; RET = IRET;
  //   STX (some bits) = {STV[31:8], STV[6:4], STV[2:0]}; VFB[31:0] = CSR_OUT

  // Notes on the sheet:
  //   contents of rom_1 (hex, n*v repeats v):
  //   768*10 5 6 10 10 7 8 58*10 9 a b 3022*10 1 2 3 4 1003*10 5 6 10 10 7 8 58*10 9 a b 3261*10
endmodule

module InterruptController (
  input  RST,
  input  RET,
  input  JMP,
  input  TRIG,
  input  WFI,
  input  RDY_IN,
  input  GRANT,
  input  EIE,
  input  CLK,
  input  SYS,
  input  BRK,
  input  [31:0] ALU,
  input  LDR,
  input  [31:0] EPC,
  input  EAM,
  input  [31:0] ISR,
  input  EPL,
  input  ILL,
  output TRAP,
  output SET,
  output RDY,
  output IRQ,
  output [31:0] CAUSE,
  output [31:0] REF
);

  wire IRG, j_k_ff_1_q, or_1_out, TRIG_t;
  wire [3:3] INTB_p2;
  wire [5:5] INTC_p2;

  J_K_Flip_Flop j_k_ff_1 (.J(1'b0), .K(1'b1), .clk(CLK), .Q(j_k_ff_1_q), .preset(TRIG));  // open: Qn, reset
  J_K_Flip_Flop j_k_ff_2 (.J(GRANT), .K(IRG), .clk(CLK), .Q(IRG), .preset(RST));  // open: Qn, reset
  Multiplexer #(.select(2), .width(32)) multiplexer_1 (
    .in0(ALU), .in1(EPC), .in2(ISR), .in3(ISR), .out(REF), .sel({TRAP, RET}));
  LED F_TRIG (.in(or_1_out));
  or or_1 (or_1_out, j_k_ff_1_q, TRIG_t);
  J_K_Flip_Flop j_k_ff_3 (.J(j_k_ff_1_q), .K(IRG), .clk(CLK), .Q(TRIG_t), .reset(RST));  // open: Qn, preset
  Register #(.trigger("high"), .width(32)) V_REF (.D(REF), .clk(1'b1));  // open: en, Q, clr
  LED F_EIE (.in(EIE));
  // PlaRom #(.Contents("0*9 2 1 1 2 2 1 0*3 1 0*6 2 1 0*3 1 1 2 2 1 2 0 0 1 1 0 2 0*12 2 0*12 2 0*10 2 0 2 0*9 1 0 1*3 0*4 1 0*3 1 0*4 1 1 0 0 1 1 0 0 1 0*3 1 0*3 1 1"), .\and (9)) INTB: pin names not known; wires that end beside it: {SYS, BRK, EIE, TRIG_t, IRG, RDY_IN, WFI, JMP, RET, RST}, {INTB_p2[3], RDY, SET, TRAP}
  // PlaRom #(.Contents("0 0 2 0*5 2 0*5 2 0*6 1*3 0 2 1*4 0*4 2 1*3 0 2 1 0 1 1 2 0 0 1 1 0 1 0*3 2 0 0 1 0*4 2 0 1 2 2 0*4 1 1 0 2 0 0 1 1 0*3 2 0 1*3 0 2 0 0 1 0*5 1 0*5 1 0*3 1 0 0 1 0*6 1 0 0 1 0 0 1 0*6 1 0*6 1 0*5 1 0*5 1 0*5 1 0*6 1 0*5 1"), .\and (13), .outputs(6)) INTC: pin names not known; wires that end beside it: {ILL, EPL, EAM, LDR, TRIG_t, BRK, SYS}, {INTC_p2[5], CAUSE[31], CAUSE[3:0]}
  LED F_TRAP (.in(TRAP));
  LED F_JMP (.in(SET));
  or or_2 (IRQ, INTB_p2[3], INTC_p2[5]);

  assign CAUSE[30:4] = {27{1'b0}};

  // Other names for the same wires on the sheet: S0 = RET; S1 = TRAP
endmodule

module cpu (
);

  wire and_1_out, and_2_out, and_3_out, and_4_out, and_5_out, binary_to_bcd_1_sup_out,
       binary_to_bcd_2_sup_out, binary_to_bcd_3_sup_out, binary_to_bcd_4_sup_out, binary_to_bcd_5_sup_out,
       binary_to_bcd_6_sup_out, binary_to_bcd_7_sup_out, binary_to_bcd_8_sup_out, binary_to_bcd_9_sup_out,
       CC, CLK, comparator_1_eq, comparator_2_eq, comparator_3_eq, INC, IO0, IO1, IWE, JMP,
       memory_interface_1_bm0, memory_interface_1_bm1, memory_interface_1_bm2, memory_interface_1_bm3,
       memory_interface_1_bus_en, memory_interface_1_bus_nrw, not_1_out, not_2_out, RDE, RST, ST, SXB, SXH;
  wire [2:0] F3;
  wire [4:0] RD, RS1, RS2;
  wire [6:0] F7;
  wire [13:0] memory_interface_1_bus_addr_2;
  wire [15:0] memory_interface_1_bus_addr, register_1_q, register_2_q;
  wire [31:0] binary_to_bcd_2_vout, binary_to_bcd_3_vout, binary_to_bcd_4_vout, binary_to_bcd_5_vout,
       binary_to_bcd_6_vout, binary_to_bcd_7_vout, binary_to_bcd_8_vout, binary_to_bcd_9_vout,
       binary_to_bcd_10_vout, bit_extender_1_out, bit_extender_2_out, INS, LR, PC, ram_1_data, register_3_q,
       rom_1_data, shifter_1_out, shifter_2_out;

  not not_1 (not_1_out, not_2_out);
  assign bit_extender_1_out = {{2{memory_interface_1_bus_addr_2[13]}}, {memory_interface_1_bus_addr_2, memory_interface_1_bus_addr}};  // Bit_Extender bit_extender_1
  _7_Segment_Display u_7_segment_display_1 ();  // open: g, f, a, b, e, d, c, dp
  _7_Segment_Display u_7_segment_display_2 ();  // open: g, f, a, b, e, d, c, dp
  // BCD_to_7_Segment_decoder bcd_to_7_segment_decoder_1: pin names not known
  // BCD_to_7_Segment_decoder bcd_to_7_segment_decoder_2: pin names not known
  binary_to_bcd binary_to_bcd_1 (
    .SUP_OUT(binary_to_bcd_1_sup_out), .VIN(binary_to_bcd_2_vout), .SUP_IN(1'b1), .SUP_0(1'b1));  // open: VOUT, DIGIT
  binary_to_bcd binary_to_bcd_2 (
    .VOUT(binary_to_bcd_2_vout), .SUP_OUT(binary_to_bcd_2_sup_out), .VIN(binary_to_bcd_3_vout),
    .SUP_IN(binary_to_bcd_1_sup_out), .SUP_0(1'b1));  // open: DIGIT
  Comparator #(.width(14)) comparator_1 (
    .a(memory_interface_1_bus_addr_2), .b({14{1'b0}}), .eq(comparator_1_eq));  // open: gt, lt
  Comparator #(.width(14)) comparator_2 (
    .a(memory_interface_1_bus_addr_2), .b(14'h200), .eq(comparator_2_eq));  // open: gt, lt
  and and_1 (and_1_out, not_1_out, comparator_2_eq);
  and and_2 (and_2_out, comparator_2_eq, not_2_out);
  Shifter #(.width(32)) shifter_1 (.in(bit_extender_1_out), .\dist (5'b00010), .out(shifter_1_out));
  Comparator #(.width(32)) comparator_3 (.a(shifter_1_out), .b(32'hc0008000), .eq(comparator_3_eq));  // open: gt, lt
  _7_Segment_Display u_7_segment_display_3 ();  // open: g, f, a, b, e, d, c, dp
  _7_Segment_Display u_7_segment_display_4 ();  // open: g, f, a, b, e, d, c, dp
  // BCD_to_7_Segment_decoder bcd_to_7_segment_decoder_3: pin names not known
  // BCD_to_7_Segment_decoder bcd_to_7_segment_decoder_4: pin names not known
  binary_to_bcd binary_to_bcd_3 (
    .VOUT(binary_to_bcd_3_vout), .SUP_OUT(binary_to_bcd_3_sup_out), .VIN(binary_to_bcd_4_vout),
    .SUP_IN(binary_to_bcd_2_sup_out), .SUP_0(1'b1));  // open: DIGIT
  ROM #(.addrWidth(16), .dataWidth(32)) rom_1 (.addr(register_1_q), .data(rom_1_data));
  Register #(.trigger("high"), .width(16)) register_1 (
    .D(memory_interface_1_bus_addr), .Q(register_1_q), .clk(comparator_1_eq));  // open: en, clr
  RAM #(.addrWidth(16), .asyncread("true"), .byteenables("byteEnables"), .dataWidth(32), .databus("bidir"), .trigger("falling")) ram_1 (
    .addr(register_2_q), .we(and_1_out), .oe(and_2_out), .clk(and_5_out), .data(ram_1_data),
    .be3(memory_interface_1_bm3), .be2(memory_interface_1_bm2), .be1(memory_interface_1_bm1),
    .be0(memory_interface_1_bm0));
  Register #(.trigger("high"), .width(16)) register_2 (
    .D(memory_interface_1_bus_addr), .Q(register_2_q), .clk(comparator_2_eq));  // open: en, clr
  and and_3 (and_3_out, ~not_2_out, comparator_3_eq);  // AND_Gate
  _7_Segment_Display u_7_segment_display_5 ();  // open: g, f, a, b, e, d, c, dp
  // BCD_to_7_Segment_decoder bcd_to_7_segment_decoder_5: pin names not known
  binary_to_bcd binary_to_bcd_4 (
    .VOUT(binary_to_bcd_4_vout), .SUP_OUT(binary_to_bcd_4_sup_out), .VIN(binary_to_bcd_5_vout),
    .SUP_IN(binary_to_bcd_3_sup_out), .SUP_0(1'b1));  // open: DIGIT
  binary_to_bcd binary_to_bcd_5 (
    .VOUT(binary_to_bcd_5_vout), .SUP_OUT(binary_to_bcd_5_sup_out), .VIN(binary_to_bcd_6_vout),
    .SUP_IN(binary_to_bcd_4_sup_out), .SUP_0(1'b1));  // open: DIGIT
  Register #(.width(32)) register_3 (.D(ram_1_data), .en(and_3_out), .clk(and_5_out), .Q(register_3_q));  // open: clr
  _7_Segment_Display u_7_segment_display_6 ();  // open: g, f, a, b, e, d, c, dp
  _7_Segment_Display u_7_segment_display_7 ();  // open: g, f, a, b, e, d, c, dp
  // BCD_to_7_Segment_decoder bcd_to_7_segment_decoder_6: pin names not known
  // BCD_to_7_Segment_decoder bcd_to_7_segment_decoder_7: pin names not known
  binary_to_bcd binary_to_bcd_6 (
    .VOUT(binary_to_bcd_6_vout), .SUP_OUT(binary_to_bcd_6_sup_out), .VIN(binary_to_bcd_7_vout),
    .SUP_IN(binary_to_bcd_5_sup_out), .SUP_0(1'b1));  // open: DIGIT
  binary_to_bcd binary_to_bcd_7 (
    .VOUT(binary_to_bcd_7_vout), .SUP_OUT(binary_to_bcd_7_sup_out), .VIN(binary_to_bcd_8_vout),
    .SUP_IN(binary_to_bcd_6_sup_out), .SUP_0(1'b1));  // open: DIGIT
  _7_Segment_Display u_7_segment_display_8 ();  // open: g, f, a, b, e, d, c, dp
  // BCD_to_7_Segment_decoder bcd_to_7_segment_decoder_8: pin names not known
  binary_to_bcd binary_to_bcd_8 (
    .VOUT(binary_to_bcd_8_vout), .SUP_OUT(binary_to_bcd_8_sup_out), .VIN(binary_to_bcd_9_vout),
    .SUP_IN(binary_to_bcd_7_sup_out), .SUP_0(1'b1));  // open: DIGIT
  assign bit_extender_2_out = {{2{memory_interface_1_bus_addr_2[13]}}, {memory_interface_1_bus_addr_2, memory_interface_1_bus_addr}};  // Bit_Extender bit_extender_2
  assign ram_1_data = and_4_out ? rom_1_data : 32'bz;  // Controlled_Buffer controlled_buffer_1
  and and_4 (and_4_out, comparator_1_eq, not_2_out);
  _7_Segment_Display u_7_segment_display_9 ();  // open: g, f, a, b, e, d, c, dp
  _7_Segment_Display u_7_segment_display_10 ();  // open: g, f, a, b, e, d, c, dp
  // BCD_to_7_Segment_decoder bcd_to_7_segment_decoder_9: pin names not known
  // BCD_to_7_Segment_decoder bcd_to_7_segment_decoder_10: pin names not known
  binary_to_bcd binary_to_bcd_9 (
    .VOUT(binary_to_bcd_9_vout), .SUP_OUT(binary_to_bcd_9_sup_out), .VIN(binary_to_bcd_10_vout),
    .SUP_IN(binary_to_bcd_8_sup_out), .SUP_0(1'b1));  // open: DIGIT
  binary_to_bcd binary_to_bcd_10 (
    .VOUT(binary_to_bcd_10_vout), .VIN(register_3_q), .SUP_IN(binary_to_bcd_9_sup_out), .SUP_0(1'b0));  // open: SUP_OUT, DIGIT
  // Probe on shifter_2_out
  Shifter #(.width(32)) shifter_2 (.in(bit_extender_2_out), .\dist (5'b00010), .out(shifter_2_out));
  // Probe on ram_1_data
  program_counter program_counter_1 (.PC(LR), .SET(JMP), .INC(INC), .CLK(CLK));  // open: ERR, ADDR
  memory_interface memory_interface_1 (
    .BUS_ADDR({memory_interface_1_bus_addr_2, memory_interface_1_bus_addr}),
    .BUS_EN(memory_interface_1_bus_en), .BM3(memory_interface_1_bm3), .BM2(memory_interface_1_bm2),
    .BM1(memory_interface_1_bm1), .BM0(memory_interface_1_bm0), .PC_INC(INC),
    .BUS_nRW(memory_interface_1_bus_nrw), .INSTR(INS), .BUS_OUT(ram_1_data), .LR(LR), .BUS_IN(ram_1_data),
    .RST(RST), .FETCH(IWE), .ST(ST), .IO0(IO0), .IO1(IO1));  // open: DIN, ADDR, DOUT
  not not_2 (not_2_out, memory_interface_1_bus_nrw);
  and and_5 (and_5_out, memory_interface_1_bus_en, CLK);
  Clock clock_1 (.out(CLK));
  // Switch switch_1: pin names not known; wires that end beside it: 1'b1, RST
  Pull_Resistor pull_resistor_1 (.node(RST));
  // Switch switch_2: pin names not known; wires that end beside it: 1'b1, CC
  Pull_Resistor pull_resistor_2 (.node(CC));
  // Switch switch_3: pin names not known; wires that end beside it: 1'b1, JMP
  Pull_Resistor pull_resistor_3 (.node(JMP));
  instruction_decoder instruction_decoder_1 (
    .RD(RD), .RS1(RS1), .RS2(RS2), .FUNCT3(F3), .FUNCT7(F7), .PC(PC), .FETCH(IWE), .SXB(SXB), .SXH(SXH),
    .IO0(IO0), .IO1(IO1), .ST_EN(ST), .RD_EN(RDE), .CLK(CLK), .COND(CC), .LR(LR), .INSTR(INS));  // open: ILL, U_to_RD, LR_to_RD, ALU_to_RD, ALU_to_PC, ALU_to_ADDR, RS1_to_ALU_X, PC_to_ALU_X, RS2_to_ALU_Y, I_to_ALU_Y, S_to_ALU_Y, B_to_ALU_Y, U_to_ALU_Y, J_to_ALU_Y, SYS_EN, AGU_EN, IMM_I, IMM_S, IMM_B, IMM_U, IMM_J
  register_file register_file_1 (.YI(RS2), .CLK(CLK), .WI(RD), .WE(RDE), .XI(RS1));  // open: Y, X, D

  // Notes on the sheet:
  //   contents of rom_1 (hex, n*v repeats v):
  //   f8010113 112223 212423 312623 412823 512a23 612c23 712e23 2812023 2912223 2a12423 2b12623 2c12823
  //   2d12a23 2e12c23 2f12e23 5012023 5112223 5212423 5312623 5412823 5512a23 5612c23 5712e23 7812023
  //   7912223 7a12423 7b12623 7c12823 7d12a23 7e12c23 7f12e23 341022f3 512023 10513 342025f3 cc000ef 12283
  //   34129073 7c12f83 7812f03 7412e83 7012e03 6c12d83 6812d03 6412c83 6012c03 5c12b83 5812b03 5412a83
  //   5012a03 4c12983 4812903 4412883 4012803 3c12783 3812703 3412683 3012603 2c12583 2812503 2412483
  //   2012403 1c12383 1812303 1412283 1012203 c12183 812103 412083 8010113 30200073 100513 50593 73 8067
  //   c00087b7 a7a023 8067 2852703 100793 f70463 8067 2c52703 c00087b7 e7a023 8067 b00793 2f58463 800007b7
  //   b78793 f59c63 5f5e7b7 c0008737 ff78793 f72023 8067 8067 2852703 100793 f71863 2c52703 c00087b7
  //   e7a023 52783 478793 f52023 8067 100613 100513 60593 73 100513 60593 73 100713 200793 100513 78593 73
  //   f706b3 e6b5b3 78713 fc0594e3 68793 100513 78593 73 f706b3 e6b5b3 78713 fa0594e3 fe1ff06f 65339*0
  //   8004117 10010113 fffc0297 f828293 30529073 fffc0297 29c28293 34129073 12b7 80028293 3042a073 8000293
  //   3002a073 30200073
endmodule

module binary_to_bcd (
  input  [31:0] VIN,
  input  SUP_IN,
  input  SUP_0,
  output [31:0] VOUT,
  output [3:0] DIGIT,
  output SUP_OUT
);

  wire comparator_1_eq, not_1_out;
  wire [31:0] divider_1_rem;

  Divider #(.width(32)) divider_1 (.a(VIN), .b(32'ha), .out(VOUT), .rem(divider_1_rem));  // open: upper
  Comparator #(.width(4)) comparator_1 (.a(divider_1_rem[3:0]), .b(4'b0000), .eq(comparator_1_eq));  // open: gt, lt
  assign DIGIT = not_1_out ? divider_1_rem[3:0] : 4'bz;  // Controlled_Buffer controlled_buffer_1
  not not_1 (not_1_out, SUP_OUT);
  and and_1 (SUP_OUT, comparator_1_eq, SUP_IN, SUP_0);

  // Notes on the sheet:
  //   SUP_IN: pull=up
  //   SUP_0: pull=up
  //   SUP_OUT: pull=up
endmodule

module memory_interface (
  input  [31:0] BUS_IN,
  input  [31:0] DOUT,
  input  [31:0] ADDR,
  input  [31:0] LR,
  input  RST,
  input  FETCH,
  input  ST,
  input  IO0,
  input  IO1,
  output PC_INC,
  output [31:0] INSTR,
  output [31:0] DIN,
  output [31:0] BUS_OUT,
  output BUS_nRW,
  output [29:0] BUS_ADDR,
  output BUS_EN,
  output BM3,
  output BM2,
  output BM1,
  output BM0
);

  wire A0, A1, decoder_1_out1, decoder_1_out2, decoder_1_out3, decoder_1_out5, decoder_1_out9,
       decoder_1_out10, decoder_1_out13, M0, M1, not_1_out, not_2_out, or_4_out;
  wire [31:0] multiplexer_3_out, multiplexer_4_out, multiplexer_5_out, multiplexer_6_out;
  wire [31:2] MAR_q;

  or or_1 (M1, IO1, FETCH);
  or or_2 (M0, IO0, FETCH);
  or or_3 (BUS_EN, IO1, IO0, FETCH);
  Multiplexer #(.width(32)) multiplexer_1 (.in0(32'h13), .in1(BUS_IN), .out(INSTR), .sel(PC_INC));
  Multiplexer #(.select(2), .width(32)) multiplexer_2 (
    .in0(BUS_IN), .in1({{8{1'b0}}, BUS_IN[31:8]}), .in2({{16{1'b0}}, BUS_IN[31:16]}),
    .in3({{24{1'b0}}, BUS_IN[31:24]}), .out(DIN), .sel({A1, A0}));
  Multiplexer #(.select(2), .width(32)) multiplexer_3 (
    .in0(DOUT), .in1({DOUT[23:0], {8{1'b0}}}), .in2({DOUT[15:0], {16{1'b0}}}), .in3({DOUT[7:0], {24{1'b0}}}),
    .out(multiplexer_3_out), .sel({A1, A0}));
  not not_1 (not_1_out, FETCH);
  or or_4 (or_4_out, IO1, IO0);
  and and_1 (BUS_nRW, or_4_out, ST);
  assign BUS_OUT = BUS_nRW ? multiplexer_3_out : 32'bz;  // Controlled_Buffer controlled_buffer_1
  nor nor_1 (PC_INC, IO1, IO0, ST, not_1_out, RST);
  not not_2 (not_2_out, PC_INC);
  Multiplexer #(.width(32)) multiplexer_4 (.in0(BUS_IN), .in1(DIN), .out(multiplexer_4_out), .sel(not_2_out));
  Multiplexer #(.width(32)) multiplexer_5 (
    .in0(multiplexer_4_out), .in1(BUS_OUT), .out(multiplexer_5_out), .sel(BUS_nRW));
  Register #(.trigger("high"), .width(32)) MDR (.D(multiplexer_5_out), .clk(1'b1));  // open: en, Q, clr
  Multiplexer #(.width(32)) multiplexer_6 (.in0(ADDR), .in1(LR), .out(multiplexer_6_out), .sel(PC_INC));
  Decoder #(.enable("false"), .select(4)) decoder_1 (
    .out1(decoder_1_out1), .out2(decoder_1_out2), .out3(decoder_1_out3), .out5(decoder_1_out5),
    .out9(decoder_1_out9), .out10(decoder_1_out10), .out13(decoder_1_out13), .sel({A1, A0, M1, M0}));  // open: out0, out4, out6, out7, out8, out11, out12, out14, out15
  Register #(.trigger("high"), .width(32)) MAR (
    .D(multiplexer_6_out), .Q({MAR_q, A1, A0}), .clk(1'b1));  // open: en, clr
  assign BUS_ADDR = BUS_EN ? MAR_q : 30'bz;  // Controlled_Buffer controlled_buffer_2
  or or_5 (BM3, decoder_1_out13, decoder_1_out10, decoder_1_out3);
  or or_6 (BM2, decoder_1_out10, decoder_1_out9, decoder_1_out3);
  or or_7 (BM1, decoder_1_out5, decoder_1_out3, decoder_1_out2);
  or or_8 (BM0, decoder_1_out3, decoder_1_out2, decoder_1_out1);

  // Other names for the same wires on the sheet: AE = BUS_EN; FE = PC_INC; OE = BUS_nRW

  // Notes on the sheet:
  //   RST: pull=up
endmodule

module program_counter (
  input  SET,
  input  INC,
  input  CLK,
  input  [31:0] ADDR,
  output ERR,
  output [31:0] PC
);

  wire or_1_out;
  wire [29:0] counter_1_q;

  and and_1 (ERR, or_1_out, SET);
  Counter #(.max('h3fffffff), .width(30)) counter_1 (
    .load(SET), .count(INC), .clk(CLK), .D(ADDR[31:2]), .Q(counter_1_q));  // open: clr, up, carry
  or or_1 (or_1_out, ADDR[1], ADDR[0]);
  Register #(.trigger("high"), .width(32)) V_PC (.D({counter_1_q, 2'b00}), .Q(PC), .clk(1'b1));  // open: en, clr
endmodule

module instruction_decoder (
  input  [31:0] INSTR,
  input  CLK,
  input  COND,
  input  [31:0] LR,
  output FETCH,
  output [31:0] IMM_I,
  output SYS_EN,
  output [4:0] RD,
  output U_to_RD,
  output [4:0] RS1,
  output ST_EN,
  output [31:0] IMM_S,
  output LR_to_RD,
  output [4:0] RS2,
  output AGU_EN,
  output [2:0] FUNCT3,
  output ALU_to_RD,
  output [6:0] FUNCT7,
  output [31:0] IMM_B,
  output ALU_to_PC,
  output [31:0] PC,
  output RD_EN,
  output ALU_to_ADDR,
  output [31:0] IMM_U,
  output RS1_to_ALU_X,
  output PC_to_ALU_X,
  output RS2_to_ALU_Y,
  output [31:0] IMM_J,
  output I_to_ALU_Y,
  output SXB,
  output S_to_ALU_Y,
  output ILL,
  output SXH,
  output B_to_ALU_Y,
  output IO0,
  output U_to_ALU_Y,
  output J_to_ALU_Y,
  output IO1
);

  wire and_1_out, and_5_out, and_6_out, decoder_1_out0, decoder_1_out1, decoder_1_out2, decoder_1_out3,
       decoder_1_out4, decoder_1_out6, decoder_1_out7, decoder_1_out9, decoder_1_out10, decoder_1_out11,
       decoder_1_out14, decoder_1_out15, decoder_1_out16, decoder_1_out17, decoder_1_out18, decoder_1_out19,
       decoder_1_out20, decoder_1_out21, decoder_1_out22, decoder_1_out23, decoder_1_out24, decoder_1_out25,
       decoder_1_out26, decoder_1_out28, decoder_1_out29, decoder_1_out30, decoder_1_out31, decoder_2_out2,
       decoder_2_out3, decoder_2_out4, decoder_2_out5, decoder_2_out6, decoder_2_out7, j_k_ff_1_q,
       j_k_ff_1_qn, nand_1_out, not_1_out, or_1_out, or_3_out, or_4_out, or_16_out, or_17_out;
  wire [1:0] V_INS_q;
  wire [4:0] OP;
  wire [11:0] bit_extender_4_out;
  wire [19:0] bit_extender_3_out;
  wire [20:0] bit_extender_1_out, bit_extender_2_out;

  LED F2 (.in(FUNCT3[2]));
  Register #(.width(32)) V_INS (
    .D(INSTR), .en(FETCH), .clk(CLK), .Q({FUNCT7, RS2, RS1, FUNCT3, RD, OP, V_INS_q}));  // open: clr
  Register #(.width(32)) V_PC (.D(LR), .en(FETCH), .clk(CLK), .Q(PC));  // open: clr
  LED F1 (.in(FUNCT3[1]));
  LED F0 (.in(FUNCT3[0]));
  LED G6 (.in(FUNCT7[6]));
  Register #(.trigger("high"), .width(5)) V_RD (.D(RD), .clk(1'b1));  // open: en, Q, clr
  LED G5 (.in(FUNCT7[5]));
  LED G4 (.in(FUNCT7[4]));
  LED G3 (.in(FUNCT7[3]));
  LED G2 (.in(FUNCT7[2]));
  Register #(.trigger("high"), .width(5)) V_RS1 (.D(RS1), .clk(1'b1));  // open: en, Q, clr
  assign bit_extender_1_out = {{20{FUNCT7[6]}}, FUNCT7[6]};  // Bit_Extender bit_extender_1
  assign bit_extender_2_out = {{20{FUNCT7[6]}}, FUNCT7[6]};  // Bit_Extender bit_extender_2
  assign bit_extender_3_out = {{19{FUNCT7[6]}}, FUNCT7[6]};  // Bit_Extender bit_extender_3
  assign bit_extender_4_out = {{11{FUNCT7[6]}}, FUNCT7[6]};  // Bit_Extender bit_extender_4
  LED G1 (.in(FUNCT7[1]));
  LED G0 (.in(FUNCT7[0]));
  LED F_COND (.in(COND));
  Register #(.trigger("high"), .width(5)) V_RS2 (.D(RS2), .clk(1'b1));  // open: en, Q, clr
  Register #(.trigger("high"), .width(32)) V_I (
    .D({bit_extender_1_out, FUNCT7[5:0], RS2}), .Q(IMM_I), .clk(1'b1));  // open: en, clr
  Register #(.trigger("high"), .width(32)) V_S (
    .D({bit_extender_2_out, FUNCT7[5:0], RD}), .Q(IMM_S), .clk(1'b1));  // open: en, clr
  Register #(.trigger("high"), .width(32)) V_B (
    .D({bit_extender_3_out, RD[0], FUNCT7[5:0], RD[4:1], 1'b0}), .Q(IMM_B), .clk(1'b1));  // open: en, clr
  Register #(.trigger("high"), .width(32)) V_U (
    .D({FUNCT7, RS2, RS1, FUNCT3, {12{1'b0}}}), .Q(IMM_U), .clk(1'b1));  // open: en, clr
  Register #(.trigger("high"), .width(32)) V_J (
    .D({bit_extender_4_out, RS1, FUNCT3, RS2[0], FUNCT7[5:0], RS2[4:1], 1'b0}), .Q(IMM_J), .clk(1'b1));  // open: en, clr
  // Probe on OP
  // Probe on RD
  // Probe on FUNCT3
  // Probe on RS1
  // Probe on RS2
  // Probe on FUNCT7
  and and_1 (and_1_out, V_INS_q[1], V_INS_q[0]);
  nand nand_1 (nand_1_out, V_INS_q[1], V_INS_q[0]);
  Decoder #(.select(5)) decoder_1 (
    .out0(decoder_1_out0), .out1(decoder_1_out1), .out2(decoder_1_out2), .out3(decoder_1_out3),
    .out4(decoder_1_out4), .out5(U_to_ALU_Y), .out6(decoder_1_out6), .out7(decoder_1_out7),
    .out8(S_to_ALU_Y), .out9(decoder_1_out9), .out10(decoder_1_out10), .out11(decoder_1_out11),
    .out12(RS2_to_ALU_Y), .out13(U_to_RD), .out14(decoder_1_out14), .out15(decoder_1_out15),
    .out16(decoder_1_out16), .out17(decoder_1_out17), .out18(decoder_1_out18), .out19(decoder_1_out19),
    .out20(decoder_1_out20), .out21(decoder_1_out21), .out22(decoder_1_out22), .out23(decoder_1_out23),
    .out24(decoder_1_out24), .out25(decoder_1_out25), .out26(decoder_1_out26), .out27(J_to_ALU_Y),
    .out28(decoder_1_out28), .out29(decoder_1_out29), .out30(decoder_1_out30), .out31(decoder_1_out31),
    .sel(OP), .en(and_1_out));
  LED R (.in(RS2_to_ALU_Y));
  LED I (.in(or_1_out));
  or or_1 (or_1_out, decoder_1_out25, decoder_1_out4, decoder_1_out0, decoder_1_out3, decoder_1_out28);
  or or_2 (ILL, decoder_1_out31, decoder_1_out30, decoder_1_out29, decoder_1_out26, decoder_1_out23, decoder_1_out22, decoder_1_out21, decoder_1_out20, decoder_1_out19, decoder_1_out18, decoder_1_out17, decoder_1_out16, decoder_1_out15, decoder_1_out14, decoder_1_out10, decoder_1_out9, decoder_1_out7, decoder_1_out6, decoder_1_out2, decoder_1_out1, nand_1_out, and_6_out, decoder_2_out7, decoder_2_out6, decoder_2_out3);
  LED S (.in(S_to_ALU_Y));
  LED B (.in(decoder_1_out24));
  or or_3 (or_3_out, J_to_ALU_Y, decoder_1_out25, decoder_1_out0, S_to_ALU_Y, B_to_ALU_Y);
  J_K_Flip_Flop j_k_ff_1 (.J(or_3_out), .K(1'b1), .clk(CLK), .Q(j_k_ff_1_q), .Qn(j_k_ff_1_qn));  // open: preset, reset
  LED U (.in(or_4_out));
  LED J (.in(J_to_ALU_Y));
  or or_4 (or_4_out, U_to_RD, U_to_ALU_Y);
  and and_2 (B_to_ALU_Y, COND, decoder_1_out24);
  xor xor_1 (FETCH, or_3_out, j_k_ff_1_qn);
  LED S1 (.in(j_k_ff_1_q));
  LED S0 (.in(j_k_ff_1_qn));
  or or_5 (LR_to_RD, J_to_ALU_Y, decoder_1_out25);
  or or_6 (ALU_to_RD, U_to_ALU_Y, RS2_to_ALU_Y, decoder_1_out4);
  or or_7 (ALU_to_PC, J_to_ALU_Y, decoder_1_out25, B_to_ALU_Y);
  or or_8 (ALU_to_ADDR, decoder_1_out0, S_to_ALU_Y);
  or or_9 (RS1_to_ALU_X, decoder_1_out25, RS2_to_ALU_Y, decoder_1_out4, decoder_1_out0, S_to_ALU_Y);
  or or_10 (PC_to_ALU_X, U_to_ALU_Y, J_to_ALU_Y, B_to_ALU_Y);
  or or_11 (I_to_ALU_Y, decoder_1_out25, decoder_1_out4, decoder_1_out0);
  or or_12 (IO0, SXB, decoder_2_out2, decoder_2_out4);
  or or_13 (IO1, SXH, decoder_2_out2, decoder_2_out5);
  and and_3 (SYS_EN, decoder_1_out28, j_k_ff_1_qn);
  and and_4 (ST_EN, S_to_ALU_Y, j_k_ff_1_qn);
  or or_14 (AGU_EN, decoder_1_out25, J_to_ALU_Y, U_to_ALU_Y, B_to_ALU_Y);
  or or_15 (RD_EN, decoder_1_out0, decoder_1_out4, RS2_to_ALU_Y, decoder_1_out25, J_to_ALU_Y, U_to_ALU_Y, U_to_RD);
  or or_16 (or_16_out, decoder_1_out0, S_to_ALU_Y);
  and and_5 (and_5_out, j_k_ff_1_qn, or_16_out);
  Decoder #(.select(3)) decoder_2 (
    .out0(SXB), .out1(SXH), .out2(decoder_2_out2), .out3(decoder_2_out3), .out4(decoder_2_out4),
    .out5(decoder_2_out5), .out6(decoder_2_out6), .out7(decoder_2_out7), .sel(FUNCT3), .en(and_5_out));
  not not_1 (not_1_out, FUNCT3[1]);
  or or_17 (or_17_out, FUNCT3[2], not_1_out, FUNCT3[0]);
  and and_6 (and_6_out, or_17_out, decoder_1_out11);
  LED LUI (.in(U_to_RD));
  LED AUIPC (.in(U_to_ALU_Y));
  LED JAL (.in(J_to_ALU_Y));
  LED JALR (.in(decoder_1_out25));
  LED BRANCH (.in(decoder_1_out24));
  LED u_OP (.in(RS2_to_ALU_Y));
  LED OP_IMM (.in(decoder_1_out4));
  LED LOAD (.in(decoder_1_out0));
  LED STORE (.in(S_to_ALU_Y));
  LED AMO (.in(decoder_1_out11));
  LED MISC_MEM (.in(decoder_1_out3));
  LED SYSTEM (.in(decoder_1_out28));

  // Other names for the same wires on the sheet: F7[6:0] = FUNCT7; F3[2:0] = FUNCT3; IWE = FETCH
endmodule

module register_file (
  input  CLK,
  input  [4:0] WI,
  input  WE,
  input  [31:0] D,
  input  [4:0] XI,
  input  [4:0] YI,
  output [31:0] X,
  output [31:0] Y
);

  wire W1, W2, W3, W4, W5, W6, W7, W8, W9, W10, W11, W12, W13, W14, W15, W16, W17, W18, W19, W20, W21, W22,
       W23, W24, W25, W26, W27, W28, W29, W30, W31;
  wire [31:0] decoder_1_out0, decoder_4_out0, L0_p2, R1, R2, R3, R4, R5, R6, R7, R8, R9, R10, R11, R12, R13,
       R14, R15, R16, R17, R18, R19, R20, R21, R22, R23, R24, R25, R26, R27, R28, R29, R30, R31;

  Decoder #(.enable("false"), .select(5)) decoder_1 (
    .out0(decoder_1_out0[0]), .out1(decoder_1_out0[1]), .out2(decoder_1_out0[2]), .out3(decoder_1_out0[3]),
    .out4(decoder_1_out0[4]), .out5(decoder_1_out0[5]), .out6(decoder_1_out0[6]), .out7(decoder_1_out0[7]),
    .out8(decoder_1_out0[8]), .out9(decoder_1_out0[9]), .out10(decoder_1_out0[10]),
    .out11(decoder_1_out0[11]), .out12(decoder_1_out0[12]), .out13(decoder_1_out0[13]),
    .out14(decoder_1_out0[14]), .out15(decoder_1_out0[15]), .out16(decoder_1_out0[16]),
    .out17(decoder_1_out0[17]), .out18(decoder_1_out0[18]), .out19(decoder_1_out0[19]),
    .out20(decoder_1_out0[20]), .out21(decoder_1_out0[21]), .out22(decoder_1_out0[22]),
    .out23(decoder_1_out0[23]), .out24(decoder_1_out0[24]), .out25(decoder_1_out0[25]),
    .out26(decoder_1_out0[26]), .out27(decoder_1_out0[27]), .out28(decoder_1_out0[28]),
    .out29(decoder_1_out0[29]), .out30(decoder_1_out0[30]), .out31(decoder_1_out0[31]), .sel(XI));
  // RGBLED L31: pin names not known; wires that end beside it: decoder_1_out0[31], L0_p2[31]
  // RGBLED L30: pin names not known; wires that end beside it: decoder_1_out0[30], L0_p2[30]
  Register #(.width(32)) register_1 (.D(D), .en(W1), .clk(CLK), .Q(R1));  // open: clr
  Register #(.width(32)) register_2 (.D(D), .en(W2), .clk(CLK), .Q(R2));  // open: clr
  Register #(.width(32)) register_3 (.D(D), .en(W3), .clk(CLK), .Q(R3));  // open: clr
  Register #(.trigger("high"), .width(32)) DATA (.D(D), .clk(1'b1));  // open: en, Q, clr
  // RGBLED L29: pin names not known; wires that end beside it: decoder_1_out0[29], L0_p2[29]
  // RGBLED L28: pin names not known; wires that end beside it: decoder_1_out0[28], L0_p2[28]
  // RGBLED L27: pin names not known; wires that end beside it: decoder_1_out0[27], L0_p2[27]
  // RGBLED L26: pin names not known; wires that end beside it: decoder_1_out0[26], L0_p2[26]
  Register #(.width(32)) register_4 (.D(D), .en(W4), .clk(CLK), .Q(R4));  // open: clr
  Register #(.width(32)) register_5 (.D(D), .en(W5), .clk(CLK), .Q(R5));  // open: clr
  Register #(.width(32)) register_6 (.D(D), .en(W6), .clk(CLK), .Q(R6));  // open: clr
  Register #(.width(32)) register_7 (.D(D), .en(W7), .clk(CLK), .Q(R7));  // open: clr
  // RGBLED L25: pin names not known; wires that end beside it: decoder_1_out0[25], L0_p2[25]
  Decoder #(.select(5)) decoder_2 (
    .out1(W1), .out2(W2), .out3(W3), .out4(W4), .out5(W5), .out6(W6), .out7(W7), .out8(W8), .out9(W9),
    .out10(W10), .out11(W11), .out12(W12), .out13(W13), .out14(W14), .out15(W15), .out16(W16), .out17(W17),
    .out18(W18), .out19(W19), .out20(W20), .out21(W21), .out22(W22), .out23(W23), .out24(W24), .out25(W25),
    .out26(W26), .out27(W27), .out28(W28), .out29(W29), .out30(W30), .out31(W31), .sel(WI), .en(WE));  // open: out0
  // RGBLED L24: pin names not known; wires that end beside it: decoder_1_out0[24], L0_p2[24]
  // RGBLED L23: pin names not known; wires that end beside it: decoder_1_out0[23], L0_p2[23]
  // RGBLED L22: pin names not known; wires that end beside it: decoder_1_out0[22], L0_p2[22]
  Register #(.width(32)) register_8 (.D(D), .en(W8), .clk(CLK), .Q(R8));  // open: clr
  Register #(.width(32)) register_9 (.D(D), .en(W9), .clk(CLK), .Q(R9));  // open: clr
  Register #(.width(32)) register_10 (.D(D), .en(W10), .clk(CLK), .Q(R10));  // open: clr
  Register #(.width(32)) register_11 (.D(D), .en(W11), .clk(CLK), .Q(R11));  // open: clr
  // RGBLED L21: pin names not known; wires that end beside it: decoder_1_out0[21], L0_p2[21]
  // RGBLED L20: pin names not known; wires that end beside it: decoder_1_out0[20], L0_p2[20]
  // RGBLED L19: pin names not known; wires that end beside it: decoder_1_out0[19], L0_p2[19]
  // RGBLED L18: pin names not known; wires that end beside it: decoder_1_out0[18], L0_p2[18]
  Register #(.width(32)) register_12 (.D(D), .en(W12), .clk(CLK), .Q(R12));  // open: clr
  Register #(.width(32)) register_13 (.D(D), .en(W13), .clk(CLK), .Q(R13));  // open: clr
  Register #(.width(32)) register_14 (.D(D), .en(W14), .clk(CLK), .Q(R14));  // open: clr
  Register #(.width(32)) register_15 (.D(D), .en(W15), .clk(CLK), .Q(R15));  // open: clr
  // RGBLED L17: pin names not known; wires that end beside it: decoder_1_out0[17], L0_p2[17]
  Multiplexer #(.select(5), .width(32)) multiplexer_1 (
    .in0({32{1'b0}}), .in1(R1), .in2(R2), .in3(R3), .in4(R4), .in5(R5), .in6(R6), .in7(R7), .in8(R8),
    .in9(R9), .in10(R10), .in11(R11), .in12(R12), .in13(R13), .in14(R14), .in15(R15), .in16(R16), .in17(R17),
    .in18(R18), .in19(R19), .in20(R20), .in21(R21), .in22(R22), .in23(R23), .in24(R24), .in25(R25),
    .in26(R26), .in27(R27), .in28(R28), .in29(R29), .in30(R30), .in31(R31), .out(X), .sel(XI));
  // RGBLED L16: pin names not known; wires that end beside it: decoder_1_out0[16], L0_p2[16]
  // RGBLED L15: pin names not known; wires that end beside it: decoder_1_out0[15], L0_p2[15]
  Register #(.width(32)) register_16 (.D(D), .en(W16), .clk(CLK), .Q(R16));  // open: clr
  Register #(.width(32)) register_17 (.D(D), .en(W17), .clk(CLK), .Q(R17));  // open: clr
  Register #(.width(32)) register_18 (.D(D), .en(W18), .clk(CLK), .Q(R18));  // open: clr
  Register #(.width(32)) register_19 (.D(D), .en(W19), .clk(CLK), .Q(R19));  // open: clr
  Register #(.trigger("high"), .width(32)) RX (.D(X), .clk(1'b1));  // open: en, Q, clr
  // RGBLED L14: pin names not known; wires that end beside it: decoder_1_out0[14], L0_p2[14]
  // RGBLED L13: pin names not known; wires that end beside it: decoder_1_out0[13], L0_p2[13]
  // RGBLED L12: pin names not known; wires that end beside it: decoder_1_out0[12], L0_p2[12]
  Register #(.width(32)) register_20 (.D(D), .en(W20), .clk(CLK), .Q(R20));  // open: clr
  Register #(.width(32)) register_21 (.D(D), .en(W21), .clk(CLK), .Q(R21));  // open: clr
  Register #(.width(32)) register_22 (.D(D), .en(W22), .clk(CLK), .Q(R22));  // open: clr
  Register #(.width(32)) register_23 (.D(D), .en(W23), .clk(CLK), .Q(R23));  // open: clr
  // RGBLED L11: pin names not known; wires that end beside it: decoder_1_out0[11], L0_p2[11]
  // RGBLED L10: pin names not known; wires that end beside it: decoder_1_out0[10], L0_p2[10]
  // RGBLED L9: pin names not known; wires that end beside it: decoder_1_out0[9], L0_p2[9]
  Register #(.width(32)) register_24 (.D(D), .en(W24), .clk(CLK), .Q(R24));  // open: clr
  Register #(.width(32)) register_25 (.D(D), .en(W25), .clk(CLK), .Q(R25));  // open: clr
  Register #(.width(32)) register_26 (.D(D), .en(W26), .clk(CLK), .Q(R26));  // open: clr
  Register #(.width(32)) register_27 (.D(D), .en(W27), .clk(CLK), .Q(R27));  // open: clr
  // RGBLED L8: pin names not known; wires that end beside it: decoder_1_out0[8], L0_p2[8]
  // RGBLED L7: pin names not known; wires that end beside it: decoder_1_out0[7], L0_p2[7]
  // RGBLED L6: pin names not known; wires that end beside it: decoder_1_out0[6], L0_p2[6]
  Register #(.width(32)) register_28 (.D(D), .en(W28), .clk(CLK), .Q(R28));  // open: clr
  Register #(.width(32)) register_29 (.D(D), .en(W29), .clk(CLK), .Q(R29));  // open: clr
  Register #(.width(32)) register_30 (.D(D), .en(W30), .clk(CLK), .Q(R30));  // open: clr
  Register #(.width(32)) register_31 (.D(D), .en(W31), .clk(CLK), .Q(R31));  // open: clr
  Multiplexer #(.select(5), .width(32)) multiplexer_2 (
    .in0({32{1'b0}}), .in1(R1), .in2(R2), .in3(R3), .in4(R4), .in5(R5), .in6(R6), .in7(R7), .in8(R8),
    .in9(R9), .in10(R10), .in11(R11), .in12(R12), .in13(R13), .in14(R14), .in15(R15), .in16(R16), .in17(R17),
    .in18(R18), .in19(R19), .in20(R20), .in21(R21), .in22(R22), .in23(R23), .in24(R24), .in25(R25),
    .in26(R26), .in27(R27), .in28(R28), .in29(R29), .in30(R30), .in31(R31), .out(Y), .sel(YI));
  // RGBLED L5: pin names not known; wires that end beside it: decoder_1_out0[5], L0_p2[5]
  // RGBLED L4: pin names not known; wires that end beside it: decoder_1_out0[4], L0_p2[4]
  Register #(.trigger("high"), .width(32)) RY (.D(Y), .clk(1'b1));  // open: en, Q, clr
  // RGBLED L3: pin names not known; wires that end beside it: decoder_1_out0[3], L0_p2[3]
  // RGBLED L2: pin names not known; wires that end beside it: decoder_1_out0[2], L0_p2[2]
  // RGBLED L1: pin names not known; wires that end beside it: decoder_1_out0[1], L0_p2[1]
  // RGBLED L0: pin names not known; wires that end beside it: decoder_1_out0[0], L0_p2[0]
  Decoder #(.enable("false"), .select(5)) decoder_3 (
    .out0(L0_p2[0]), .out1(L0_p2[1]), .out2(L0_p2[2]), .out3(L0_p2[3]), .out4(L0_p2[4]), .out5(L0_p2[5]),
    .out6(L0_p2[6]), .out7(L0_p2[7]), .out8(L0_p2[8]), .out9(L0_p2[9]), .out10(L0_p2[10]), .out11(L0_p2[11]),
    .out12(L0_p2[12]), .out13(L0_p2[13]), .out14(L0_p2[14]), .out15(L0_p2[15]), .out16(L0_p2[16]),
    .out17(L0_p2[17]), .out18(L0_p2[18]), .out19(L0_p2[19]), .out20(L0_p2[20]), .out21(L0_p2[21]),
    .out22(L0_p2[22]), .out23(L0_p2[23]), .out24(L0_p2[24]), .out25(L0_p2[25]), .out26(L0_p2[26]),
    .out27(L0_p2[27]), .out28(L0_p2[28]), .out29(L0_p2[29]), .out30(L0_p2[30]), .out31(L0_p2[31]), .sel(YI));
  Decoder #(.enable("false"), .select(5)) decoder_4 (
    .out0(decoder_4_out0[0]), .out1(decoder_4_out0[1]), .out2(decoder_4_out0[2]), .out3(decoder_4_out0[3]),
    .out4(decoder_4_out0[4]), .out5(decoder_4_out0[5]), .out6(decoder_4_out0[6]), .out7(decoder_4_out0[7]),
    .out8(decoder_4_out0[8]), .out9(decoder_4_out0[9]), .out10(decoder_4_out0[10]),
    .out11(decoder_4_out0[11]), .out12(decoder_4_out0[12]), .out13(decoder_4_out0[13]),
    .out14(decoder_4_out0[14]), .out15(decoder_4_out0[15]), .out16(decoder_4_out0[16]),
    .out17(decoder_4_out0[17]), .out18(decoder_4_out0[18]), .out19(decoder_4_out0[19]),
    .out20(decoder_4_out0[20]), .out21(decoder_4_out0[21]), .out22(decoder_4_out0[22]),
    .out23(decoder_4_out0[23]), .out24(decoder_4_out0[24]), .out25(decoder_4_out0[25]),
    .out26(decoder_4_out0[26]), .out27(decoder_4_out0[27]), .out28(decoder_4_out0[28]),
    .out29(decoder_4_out0[29]), .out30(decoder_4_out0[30]), .out31(decoder_4_out0[31]), .sel(WI));

  // Other names for the same wires on the sheet: DI[31:0] = D
endmodule

module alu (
);

  wire alu_addsub_bitops_1_cout, alu_neq_zero_1_nz, alu_neq_zero_2_nz, and_1_out, and_2_out, and_3_out,
       and_4_out, and_5_out, and_6_out, and_10_out, and_11_out, and_12_out, and_13_out, and_14_out,
       and_15_out, and_17_out, and_18_out, and_19_out, and_20_out, and_21_out, and_23_out, button_1_out,
       button_2_out, button_3_out, clock_1_out, clock_2_out, d_ff_2_q, d_ff_2_qn, d_ff_3_q, d_ff_4_q,
       d_ff_5_q, dipswitch_1_p1, dipswitch_1_p2, dipswitch_2_p1, dipswitch_2_p2, dipswitch_3_p1, j_k_ff_1_q,
       j_k_ff_1_qn, j_k_ff_2_q, j_k_ff_2_qn, multiplexer_4_out, multiplexer_6_out, nor_1_out, nor_2_out,
       not_1_out, not_2_out, not_3_out, not_4_out, not_5_out, not_6_out, not_8_out, or_1_out, or_3_out,
       or_4_out, or_5_out, or_6_out, or_7_out, or_8_out, or_9_out, s_r_ff_1_q, xnor_1_out, xor_3_out,
       xor_4_out, xor_5_out, xor_6_out, xor_8_out, xor_9_out;
  wire [0:0] and_22_out, and_24_out, d_ff_1_q, nand_3_out, not_7_out, not_9_out, xor_7_out;
  wire [7:0] counter_1_q, counter_2_q;
  wire [15:0] adder_1_out_2, controlled_buffer_2_out, controlled_buffer_3_out, controlled_buffer_4_out,
       idt7216_1_p, idt7216_2_p, idt7216_3_p, idt7216_4_p, register_1_q, register_5_q;
  wire [30:0] register_8_q_2, register_9_q_2;
  wire [31:0] adder_1_out, adder_3_out, adder_4_out, alu_addsub_bitops_2_r, and_7_out, and_8_out, and_9_out,
       and_25_out, bit_extender_1_out, bit_extender_2_out, bit_extender_7_out, divider_1_out, divider_1_rem,
       divider_2_out, divider_2_rem, multiplexer_1_out, multiplexer_2_out, multiplexer_3_out,
       multiplexer_9_out, multiplexer_10_out, multiplexer_11_out, multiplier_1_cout, multiplier_1_out,
       multiplier_2_cout, nand_1_out, nand_2_out, or_2_out, register_2_q, register_3_q, register_4_q,
       subtractor_2_out, xor_1_out, xor_2_out;
  wire [31:16] controlled_buffer_1_out;
  wire [31:31] register_8_q, register_9_q;
  wire [32:0] adder_2_out, bit_extender_3_out, bit_extender_4_out, multiplier_3_cout, multiplier_3_out,
       register_6_q, subtractor_1_out;
  wire [32:32] and_16_out, multiplexer_8_out;
  wire [63:0] bit_extender_5_out, bit_extender_6_out, multiplexer_5_out, multiplexer_7_out;
  wire [63:1] alu_addsub_bitops_1_r, register_7_q;
  wire [63:31] register_7_q_2;

  Button button_1 (.out(button_1_out));
  // DipSwitch #(.number(2)) dipswitch_1: pin names not known; wires that end beside it: dipswitch_1_p1, dipswitch_1_p2
  xnor xnor_1 (xnor_1_out, j_k_ff_2_qn, j_k_ff_1_qn);
  J_K_Flip_Flop #(.trigger("falling")) j_k_ff_1 (
    .J(xnor_1_out), .K(xnor_1_out), .clk(button_1_out), .Q(j_k_ff_1_q), .Qn(j_k_ff_1_qn));  // open: preset, reset
  assign controlled_buffer_1_out = and_1_out ? {16{1'b0}} : 16'bz;  // Controlled_Buffer controlled_buffer_1
  assign controlled_buffer_2_out = and_1_out ? 16'hff9c : 16'bz;  // Controlled_Buffer controlled_buffer_2
  assign controlled_buffer_3_out = and_1_out ? 16'h7b : 16'bz;  // Controlled_Buffer controlled_buffer_3
  assign controlled_buffer_4_out = and_1_out ? 16'h7b : 16'bz;  // Controlled_Buffer controlled_buffer_4
  and and_1 (and_1_out, j_k_ff_1_qn, j_k_ff_2_qn);
  and and_2 (and_2_out, button_1_out, j_k_ff_1_qn, j_k_ff_2_qn);
  IDT7216 idt7216_1 (
    .Yout(controlled_buffer_1_out), .P(idt7216_1_p), .X({16{1'b1}}), .CLK_XY(and_2_out),
    .Yin(controlled_buffer_1_out), .OELn(and_1_out));
  IDT7216 idt7216_2 (
    .Yout(controlled_buffer_2_out), .P(idt7216_2_p), .X({16{1'b0}}), .CLK_XY(and_2_out),
    .Yin(controlled_buffer_2_out), .OELn(and_1_out));
  IDT7216 idt7216_3 (
    .Yout(controlled_buffer_3_out), .P(idt7216_3_p), .X({16{1'b1}}), .CLK_XY(and_2_out),
    .Yin(controlled_buffer_3_out), .OELn(and_1_out));
  IDT7216 idt7216_4 (
    .Yout(controlled_buffer_4_out), .P(idt7216_4_p), .X(16'hff9c), .CLK_XY(and_2_out),
    .Yin(controlled_buffer_4_out), .OELn(and_1_out));
  and and_3 (and_3_out, j_k_ff_1_q, dipswitch_1_p1, j_k_ff_2_q);
  and and_4 (and_4_out, button_1_out, j_k_ff_1_q);
  or or_1 (or_1_out, j_k_ff_1_qn, not_1_out);
  not not_1 (not_1_out, dipswitch_1_p1);
  and and_5 (and_5_out, dipswitch_1_p2, 1'b0);
  and and_6 (and_6_out, j_k_ff_2_q, or_1_out);
  LED led_1 (.in(and_6_out));
  J_K_Flip_Flop #(.trigger("falling")) j_k_ff_2 (
    .J(j_k_ff_1_q), .K(or_1_out), .clk(button_1_out), .Q(j_k_ff_2_q), .Qn(j_k_ff_2_qn));  // open: preset, reset
  assign bit_extender_1_out = {{31{and_5_out}}, and_5_out};  // Bit_Extender bit_extender_1
  assign bit_extender_2_out = {{31{1'b1}}, 1'b1};  // Bit_Extender bit_extender_2
  assign nand_1_out = ~(32'hffffff9c & bit_extender_1_out);  // NAND_Gate nand_1, 32 bits wide
  assign nand_2_out = ~(bit_extender_2_out & 32'h7b);  // NAND_Gate nand_2, 32 bits wide
  Multiplexer #(.width(32)) multiplexer_1 (
    .in0({controlled_buffer_1_out, idt7216_4_p}), .in1(adder_1_out), .out(multiplexer_1_out), .sel(and_3_out));
  Multiplexer #(.width(32)) multiplexer_2 (
    .in0({idt7216_3_p, controlled_buffer_3_out}), .in1(nand_1_out), .out(multiplexer_2_out), .sel(and_3_out));
  Multiplexer #(.width(32)) multiplexer_3 (
    .in0({idt7216_2_p, controlled_buffer_2_out}), .in1(nand_2_out), .out(multiplexer_3_out), .sel(and_3_out));
  // Probe on controlled_buffer_1_out
  // Probe on idt7216_1_p
  // Probe on controlled_buffer_2_out
  // Probe on idt7216_2_p
  // Probe on controlled_buffer_3_out
  // Probe on idt7216_3_p
  // Probe on controlled_buffer_4_out
  // Probe on idt7216_4_p
  D_Flip_Flop d_ff_1 (.D(and_3_out), .clk(and_4_out), .Q(d_ff_1_q[0]));  // open: Qn, preset, reset
  Register #(.trigger("high"), .width(16)) register_1 (
    .D(idt7216_1_p), .clk(and_4_out), .Q(register_1_q));  // open: en, clr
  Register #(.width(32)) register_2 (.D(multiplexer_1_out), .clk(and_4_out), .Q(register_2_q));  // open: en, clr
  Register #(.width(32)) register_3 (.D(multiplexer_2_out), .clk(and_4_out), .Q(register_3_q));  // open: en, clr
  Register #(.width(32)) register_4 (.D(multiplexer_3_out), .clk(and_4_out), .Q(register_4_q));  // open: en, clr
  Register #(.trigger("high"), .width(16)) register_5 (
    .D(controlled_buffer_4_out), .clk(and_4_out), .Q(register_5_q));  // open: en, clr
  assign xor_1_out = register_3_q ^ register_4_q;  // XOR_Gate xor_1, 32 bits wide
  assign and_7_out = register_4_q & register_3_q;  // AND_Gate and_7, 32 bits wide
  assign and_8_out = register_4_q & register_2_q;  // AND_Gate and_8, 32 bits wide
  assign and_9_out = register_3_q & register_2_q;  // AND_Gate and_9, 32 bits wide
  assign xor_2_out = register_2_q ^ xor_1_out;  // XOR_Gate xor_2, 32 bits wide
  assign or_2_out = and_7_out | and_8_out | and_9_out;  // OR_Gate or_2, 32 bits wide
  Multiplier #(.mode("twosComplement"), .width(32)) multiplier_1 (
    .a(32'hffffff9c), .b(32'h7b), .out(multiplier_1_out), .cout(multiplier_1_cout));  // open: cin
  Multiplier #(.width(32)) multiplier_2 (.a(32'hffffff9c), .b(32'h7b), .cout(multiplier_2_cout));  // open: out, cin
  assign bit_extender_3_out = {{1{1'b1}}, 32'hffffff9c};  // Bit_Extender bit_extender_3
  assign bit_extender_4_out = {{1{1'b0}}, 32'h7b};  // Bit_Extender bit_extender_4
  Divider #(.width(32)) divider_1 (
    .a(32'hffffff9c), .b(32'h7b), .out(divider_1_out), .rem(divider_1_rem));  // open: upper
  Divider #(.mode("twosComplement"), .width(32)) divider_2 (
    .a(32'hffffff9c), .b(32'h7b), .out(divider_2_out), .rem(divider_2_rem));  // open: upper
  Adder #(.width(48)) adder_1 (
    .a({register_1_q, xor_2_out}), .b({{15{1'b0}}, or_2_out, d_ff_1_q[0]}),
    .out({adder_1_out, adder_1_out_2}), .cin(d_ff_1_q[0]));  // open: cout
  Multiplier #(.mode("twosComplement"), .width(33)) multiplier_3 (
    .a(bit_extender_3_out), .b(bit_extender_4_out), .out(multiplier_3_out), .cout(multiplier_3_cout));  // open: cin
  // Probe on multiplier_1_out
  // Probe on multiplier_1_cout
  // Probe on multiplier_2_cout
  // Probe on {multiplier_3_cout[30:0], multiplier_3_out[32]}
  // Probe on divider_1_out
  // Probe on divider_1_rem
  // Probe on divider_2_out
  // Probe on divider_2_rem
  // Probe on adder_1_out
  // Probe on {adder_1_out[15:0], adder_1_out_2}
  // Probe on {adder_1_out_2, register_5_q}
  Button button_2 (.out(button_2_out));
  Clock clock_1 (.out(clock_1_out));
  // DipSwitch #(.number(2)) dipswitch_2: pin names not known; wires that end beside it: dipswitch_2_p1, dipswitch_2_p2
  Button button_3 (.out(button_3_out));
  // DipSwitch #(.number(2)) dipswitch_3: pin names not known; wires that end beside it: dipswitch_3_p1
  S_R_Flip_Flop s_r_ff_1 (
    .S(button_2_out), .R(and_17_out), .clk(clock_1_out), .Q(s_r_ff_1_q), .reset(and_17_out));  // open: Qn, preset
  not not_2 (not_2_out, and_14_out);
  and and_10 (and_10_out, not_2_out, clock_2_out);
  Clock clock_2 (.out(clock_2_out));
  and and_11 (and_11_out, clock_1_out, s_r_ff_1_q);
  and and_12 (and_12_out, dipswitch_2_p1, 1'b1);
  assign bit_extender_5_out = {{32{and_12_out}}, 32'hffffff9c};  // Bit_Extender bit_extender_5
  and and_13 (and_13_out, dipswitch_2_p1, 1'b0);
  LED led_2 (.in(and_14_out));
  and and_14 (and_14_out, counter_1_q[5], counter_1_q[0]);
  Counter counter_1 (
    .clr(button_3_out), .load(and_14_out), .clk(and_10_out), .D({8{1'b0}}), .Q(counter_1_q));  // open: up, count, carry
  and and_15 (and_15_out, dipswitch_3_p1, 1'b1);
  assign bit_extender_6_out = {{32{and_15_out}}, 32'hffffff9c};  // Bit_Extender bit_extender_6
  and and_16 (and_16_out[32], dipswitch_3_p1, 1'b0);
  LED led_3 (.in(and_17_out));
  and and_17 (and_17_out, counter_2_q[5], counter_2_q[0]);
  Counter counter_2 (
    .clr(button_2_out), .load(and_17_out), .clk(and_11_out), .D({8{1'b0}}), .Q(counter_2_q));  // open: up, count, carry
  Multiplexer multiplexer_4 (.in0(xor_3_out), .in1(and_12_out), .out(multiplexer_4_out), .sel(not_3_out));
  Multiplexer #(.width(64)) multiplexer_5 (
    .in0({alu_addsub_bitops_1_r, 1'b0}), .in1(bit_extender_5_out), .out(multiplexer_5_out), .sel(not_3_out));
  not not_3 (not_3_out, or_3_out);
  or or_3 (or_3_out, counter_1_q[5], counter_1_q[4], counter_1_q[3], counter_1_q[2], counter_1_q[1], counter_1_q[0]);
  not not_4 (not_4_out, not_5_out);
  Multiplexer multiplexer_6 (.in0(multiplexer_8_out[32]), .in1(and_15_out), .out(multiplexer_6_out), .sel(not_5_out));
  Multiplexer #(.width(64)) multiplexer_7 (
    .in0({register_7_q, 1'b0}), .in1(bit_extender_6_out), .out(multiplexer_7_out), .sel(not_5_out));
  not not_5 (not_5_out, or_4_out);
  or or_4 (or_4_out, counter_2_q[5], counter_2_q[4], counter_2_q[3], counter_2_q[2], counter_2_q[1], counter_2_q[0]);
  and and_18 (and_18_out, alu_neq_zero_1_nz, d_ff_2_qn);
  D_Flip_Flop d_ff_2 (.D(nor_1_out), .clk(and_10_out), .Q(d_ff_2_q), .Qn(d_ff_2_qn));  // open: preset, reset
  nor nor_1 (nor_1_out, and_18_out, not_3_out);
  D_Flip_Flop d_ff_3 (.D(multiplexer_4_out), .clk(and_10_out), .Q(d_ff_3_q));  // open: Qn, preset, reset
  Register #(.width(64)) register_6 (
    .D(multiplexer_5_out), .clk(and_10_out), .Q({register_6_q, alu_addsub_bitops_1_r[31:1]}));  // open: en, clr
  or or_5 (or_5_out, not_6_out, d_ff_4_q);
  D_Flip_Flop d_ff_4 (.D(and_19_out), .clk(and_11_out), .Q(d_ff_4_q));  // open: Qn, preset, reset
  and and_19 (and_19_out, or_5_out, not_4_out);
  D_Flip_Flop d_ff_5 (.D(multiplexer_6_out), .clk(and_11_out), .Q(d_ff_5_q));  // open: Qn, preset, reset
  Register #(.width(64)) register_7 (
    .D(multiplexer_7_out), .clk(and_11_out), .Q({register_7_q_2, register_7_q[31:1]}));  // open: en, clr
  alu_neq_zero alu_neq_zero_1 (.NZ(alu_neq_zero_1_nz), .X(register_6_q));
  xor xor_3 (xor_3_out, xor_9_out, xor_8_out);
  not not_6 (not_6_out, alu_neq_zero_2_nz);
  xor xor_4 (xor_4_out, and_15_out, d_ff_5_q);
  xor xor_5 (xor_5_out, d_ff_5_q, and_16_out[32]);
  xor xor_6 (xor_6_out, and_12_out, d_ff_3_q);
  xor xor_7 (xor_7_out[0], d_ff_3_q, and_13_out);
  not not_7 (not_7_out[0], xor_7_out[0]);
  xor xor_8 (xor_8_out, register_6_q[32], and_13_out);
  // Probe on alu_addsub_bitops_2_r
  or or_6 (or_6_out, d_ff_4_q, xor_4_out);
  and and_20 (and_20_out, alu_neq_zero_1_nz, or_7_out);
  or or_7 (or_7_out, d_ff_2_q, xor_6_out);
  alu_neq_zero alu_neq_zero_2 (.NZ(alu_neq_zero_2_nz), .X(register_7_q_2));
  and and_21 (and_21_out, alu_neq_zero_2_nz, or_6_out);
  Subtractor #(.width(33)) subtractor_1 (
    .a(register_7_q_2), .b({and_16_out[32], 32'h7b}), .out(subtractor_1_out));  // open: bin, bout
  Adder #(.width(33)) adder_2 (.a(register_7_q_2), .b({and_16_out[32], 32'h7b}), .out(adder_2_out));  // open: cin, cout
  Subtractor #(.width(32)) subtractor_2 (
    .a(register_7_q_2[63:32]), .b(32'h7b), .out(subtractor_2_out));  // open: bin, bout
  Adder #(.width(32)) adder_3 (.a(register_7_q_2[63:32]), .b(32'h7b), .out(adder_3_out));  // open: cin, cout
  alu_addsub_bitops alu_addsub_bitops_1 (
    .R(alu_addsub_bitops_1_r[63:32]), .Cout(alu_addsub_bitops_1_cout), .X(register_6_q[31:0]), .Y(32'h7b),
    .Cin(not_7_out[0]), .SEL({2'b01, xor_7_out[0]}));
  Multiplexer #(.width(33)) multiplexer_8 (
    .in0(subtractor_1_out), .in1(adder_2_out), .out({multiplexer_8_out[32], register_7_q[63:32]}),
    .sel(xor_5_out));
  Multiplexer #(.width(32)) multiplexer_9 (
    .in0(subtractor_2_out), .in1(adder_3_out), .out(multiplexer_9_out), .sel(xor_5_out));
  Multiplexer #(.width(32)) multiplexer_10 (
    .in0(register_7_q_2[63:32]), .in1(multiplexer_9_out), .out(multiplexer_10_out), .sel(and_21_out));
  xor xor_9 (xor_9_out, not_7_out[0], alu_addsub_bitops_1_cout);
  not not_8 (not_8_out, and_21_out);
  and and_22 (and_22_out[0], and_21_out, not_9_out[0]);
  not not_9 (not_9_out[0], xor_5_out);
  Register #(.width(32)) register_8 (
    .D({register_8_q_2, not_9_out[0]}), .clk(and_11_out), .Q({register_8_q[31], register_8_q_2}));  // open: en, clr
  Register #(.width(32)) register_9 (
    .D({register_9_q_2, not_7_out[0]}), .clk(and_10_out), .Q({register_9_q[31], register_9_q_2}));  // open: en, clr
  and and_23 (and_23_out, and_20_out, dipswitch_2_p2);
  or or_8 (or_8_out, not_8_out, and_22_out[0]);
  and and_24 (and_24_out[0], and_20_out, not_7_out[0]);
  assign bit_extender_7_out = {{31{and_23_out}}, and_23_out};  // Bit_Extender bit_extender_7
  nor nor_2 (nor_2_out, and_20_out, dipswitch_2_p2);
  Adder #(.width(32)) adder_4 (
    .a({32{1'b0}}), .b({register_8_q_2, and_22_out[0]}), .out(adder_4_out), .cin(or_8_out));  // open: cout
  Multiplexer #(.width(32)) multiplexer_11 (
    .in0({register_9_q_2, and_24_out[0]}), .in1(register_6_q[32:1]), .out(multiplexer_11_out),
    .sel(dipswitch_2_p2));
  assign and_25_out = bit_extender_7_out & 32'h7b;  // AND_Gate and_25, 32 bits wide
  or or_9 (or_9_out, nor_2_out, not_7_out[0]);
  nand nand_3 (nand_3_out[0], dipswitch_2_p2, not_7_out[0]);
  // Probe on adder_4_out
  // Probe on multiplexer_10_out
  alu_addsub_bitops alu_addsub_bitops_2 (
    .R(alu_addsub_bitops_2_r), .X(multiplexer_11_out), .Y(and_25_out), .Cin(or_9_out),
    .SEL({2'b01, nand_3_out[0]}));  // open: Cout

  // Notes on the sheet:
  //   aA
  //   aA'
  //   aB
  //   aB'
  //   bA
  //   bA'
  //   bB
  //   bB'
  //   MULHU
  //   MULH[SU]
  //   MUL
  //   dividant_sign
  //   remainder_sign
  //   divisor_sign
endmodule

module alu_neq_zero (
  input  [32:0] X,
  output NZ
);

  wire nor_1_out, nor_2_out, nor_3_out, nor_4_out, nor_5_out, nor_6_out, nor_7_out, nor_8_out;

  nor nor_1 (nor_1_out, X[0], X[1], X[2], X[3], X[4]);
  nor nor_2 (nor_2_out, X[5], X[6], X[7], X[8], X[9]);
  nor nor_3 (nor_3_out, X[10], X[11], X[12], X[13], X[14]);
  nor nor_4 (nor_4_out, X[15], X[16], X[17], X[18], X[19]);
  nor nor_5 (nor_5_out, X[20], X[21], X[22], X[23], X[24]);
  nor nor_6 (nor_6_out, X[25], X[26], X[27], X[28], X[29]);
  nor nor_7 (nor_7_out, X[30], X[31], X[32], 1'b0, 1'b0);
  nor nor_8 (nor_8_out, 1'b0, 1'b0, 1'b0, 1'b0, 1'b0);
  nand nand_1 (NZ, nor_1_out, nor_2_out, nor_3_out, nor_4_out, nor_5_out, nor_6_out, nor_7_out, nor_8_out);
endmodule

module alu_32bit_cmp (
  input  [31:0] P,
  input  [31:0] Q,
  output EQ,
  output LTU,
  output LT
);

  wire sn74as885_5_p_gt_q;
  wire [7:0] sn74as885_1_p_gt_q, sn74as885_1_p_lt_q;

  SN74AS885 sn74as885_1 (
    .P_gt_Q(sn74as885_1_p_gt_q[0]), .P_lt_Q(sn74as885_1_p_lt_q[0]), .Q(Q[7:0]), .P_gt_Q_in(1'b0),
    .P_lt_Q_in(1'b0), .LAn(1'b1), .P(P[7:0]), .PLE(1'b1));
  SN74AS885 sn74as885_2 (
    .P_gt_Q(sn74as885_1_p_gt_q[1]), .P_lt_Q(sn74as885_1_p_lt_q[1]), .Q(Q[15:8]), .P_gt_Q_in(1'b0),
    .P_lt_Q_in(1'b0), .LAn(1'b1), .P(P[15:8]), .PLE(1'b1));
  SN74AS885 sn74as885_3 (
    .P_gt_Q(sn74as885_1_p_gt_q[2]), .P_lt_Q(sn74as885_1_p_lt_q[2]), .Q(Q[23:16]), .P_gt_Q_in(1'b0),
    .P_lt_Q_in(1'b0), .LAn(1'b1), .P(P[23:16]), .PLE(1'b1));
  SN74AS885 sn74as885_4 (
    .P_gt_Q(sn74as885_1_p_gt_q[7]), .P_lt_Q(sn74as885_1_p_lt_q[7]), .Q(Q[31:24]), .P_gt_Q_in(1'b0),
    .P_lt_Q_in(1'b0), .LAn(1'b1), .P(P[31:24]), .PLE(1'b1));
  SN74AS885 sn74as885_5 (
    .P_gt_Q(sn74as885_5_p_gt_q), .P_lt_Q(LTU), .Q({sn74as885_1_p_lt_q[7], 4'b0000, sn74as885_1_p_lt_q[2:0]}),
    .P_gt_Q_in(1'b0), .P_lt_Q_in(1'b0), .LAn(1'b1),
    .P({sn74as885_1_p_gt_q[7], 4'b0000, sn74as885_1_p_gt_q[2:0]}), .PLE(1'b1));
  nor nor_1 (EQ, sn74as885_5_p_gt_q, LTU);
  Multiplexer #(.select(3)) multiplexer_1 (
    .in0(1'b0), .in1(1'b1), .in2(1'b1), .in3(1'b1), .in4(1'b0), .in5(1'b0), .in6(1'b0), .in7(1'b1), .out(LT),
    .sel({Q[31], P[31], LTU}));
endmodule
module alu_addsub_bitops (
  input  [2:0] SEL,
  input  Cin,
  input  [31:0] X,
  input  [31:0] Y,
  output [31:0] R,
  output Cout
);

  wire alu_carry_lookahead_generator_1_c1, alu_carry_lookahead_generator_1_c2,
       alu_carry_lookahead_generator_1_c3, alu_carry_lookahead_generator_1_c4,
       alu_carry_lookahead_generator_1_c5, alu_carry_lookahead_generator_1_c6,
       alu_carry_lookahead_generator_1_c7, decoder_1_out2, decoder_1_out3, decoder_1_out4, decoder_1_out5,
       decoder_1_out6, sn74f381_1_gbar, sn74f381_1_pbar, sn74f381_2_gbar, sn74f381_2_pbar, sn74f381_3_gbar,
       sn74f381_3_pbar, sn74f381_4_gbar, sn74f381_4_pbar, sn74f381_5_gbar, sn74f381_5_pbar, sn74f381_6_gbar,
       sn74f381_6_pbar, sn74f381_7_gbar, sn74f381_7_pbar;

  LED A_minus_B (.in(decoder_1_out2));
  LED A_plus_B (.in(decoder_1_out3));
  LED A_xor_B (.in(decoder_1_out4));
  LED A_or_B (.in(decoder_1_out5));
  LED A_and_B (.in(decoder_1_out6));
  Decoder #(.enable("false"), .select(3)) decoder_1 (
    .out2(decoder_1_out2), .out3(decoder_1_out3), .out4(decoder_1_out4), .out5(decoder_1_out5),
    .out6(decoder_1_out6), .sel(SEL));  // open: out0, out1, out7
  Register #(.trigger("high"), .width(32)) VX (.D(X), .clk(1'b1));  // open: en, Q, clr
  Register #(.trigger("high"), .width(32)) VY (.D(Y), .clk(1'b1));  // open: en, Q, clr
  Register #(.trigger("high"), .width(32)) VR (.D(R), .clk(1'b1));  // open: en, Q, clr
  LED F_Cin (.in(Cin));
  SN74F381 sn74f381_1 (
    .F2(R[2]), .F3(R[3]), .Pbar(sn74f381_1_pbar), .Gbar(sn74f381_1_gbar), .F0(R[0]), .F1(R[1]), .S0(SEL[0]),
    .S1(SEL[1]), .S2(SEL[2]), .B0(Y[0]), .A2(X[2]), .B3(Y[3]), .A3(X[3]), .A0(X[0]), .Cin(Cin), .B1(Y[1]),
    .A1(X[1]), .B2(Y[2]));  // open: Cout
  SN74F381 sn74f381_2 (
    .F2(R[18]), .F3(R[19]), .Pbar(sn74f381_2_pbar), .Gbar(sn74f381_2_gbar), .F0(R[16]), .F1(R[17]),
    .S0(SEL[0]), .S1(SEL[1]), .S2(SEL[2]), .B0(Y[16]), .A2(X[18]), .B3(Y[19]), .A3(X[19]), .A0(X[16]),
    .Cin(alu_carry_lookahead_generator_1_c4), .B1(Y[17]), .A1(X[17]), .B2(Y[18]));  // open: Cout
  SN74F381 sn74f381_3 (
    .F2(R[6]), .F3(R[7]), .Pbar(sn74f381_3_pbar), .Gbar(sn74f381_3_gbar), .F0(R[4]), .F1(R[5]), .S0(SEL[0]),
    .S1(SEL[1]), .S2(SEL[2]), .B0(Y[4]), .A2(X[6]), .B3(Y[7]), .A3(X[7]), .A0(X[4]),
    .Cin(alu_carry_lookahead_generator_1_c1), .B1(Y[5]), .A1(X[5]), .B2(Y[6]));  // open: Cout
  alu_carry_lookahead_generator alu_carry_lookahead_generator_1 (
    .C5(alu_carry_lookahead_generator_1_c5), .C6(alu_carry_lookahead_generator_1_c6),
    .C7(alu_carry_lookahead_generator_1_c7), .C1(alu_carry_lookahead_generator_1_c1),
    .C2(alu_carry_lookahead_generator_1_c2), .C3(alu_carry_lookahead_generator_1_c3),
    .C4(alu_carry_lookahead_generator_1_c4), .P4(sn74f381_2_pbar), .G4(sn74f381_2_gbar),
    .P5(sn74f381_4_pbar), .G5(sn74f381_4_gbar), .P6(sn74f381_6_pbar), .G6(sn74f381_6_gbar), .C0(Cin),
    .P0(sn74f381_1_pbar), .G0(sn74f381_1_gbar), .P1(sn74f381_3_pbar), .G1(sn74f381_3_gbar),
    .P2(sn74f381_5_pbar), .G2(sn74f381_5_gbar), .P3(sn74f381_7_pbar), .G3(sn74f381_7_gbar));
  SN74F381 sn74f381_4 (
    .F2(R[22]), .F3(R[23]), .Pbar(sn74f381_4_pbar), .Gbar(sn74f381_4_gbar), .F0(R[20]), .F1(R[21]),
    .S0(SEL[0]), .S1(SEL[1]), .S2(SEL[2]), .B0(Y[20]), .A2(X[22]), .B3(Y[23]), .A3(X[23]), .A0(X[20]),
    .Cin(alu_carry_lookahead_generator_1_c5), .B1(Y[21]), .A1(X[21]), .B2(Y[22]));  // open: Cout
  SN74F381 sn74f381_5 (
    .F2(R[10]), .F3(R[11]), .Pbar(sn74f381_5_pbar), .Gbar(sn74f381_5_gbar), .F0(R[8]), .F1(R[9]),
    .S0(SEL[0]), .S1(SEL[1]), .S2(SEL[2]), .B0(Y[8]), .A2(X[10]), .B3(Y[11]), .A3(X[11]), .A0(X[8]),
    .Cin(alu_carry_lookahead_generator_1_c2), .B1(Y[9]), .A1(X[9]), .B2(Y[10]));  // open: Cout
  SN74F381 sn74f381_6 (
    .F2(R[26]), .F3(R[27]), .Pbar(sn74f381_6_pbar), .Gbar(sn74f381_6_gbar), .F0(R[24]), .F1(R[25]),
    .S0(SEL[0]), .S1(SEL[1]), .S2(SEL[2]), .B0(Y[24]), .A2(X[26]), .B3(Y[27]), .A3(X[27]), .A0(X[24]),
    .Cin(alu_carry_lookahead_generator_1_c6), .B1(Y[25]), .A1(X[25]), .B2(Y[26]));  // open: Cout
  SN74F381 sn74f381_7 (
    .F2(R[14]), .F3(R[15]), .Pbar(sn74f381_7_pbar), .Gbar(sn74f381_7_gbar), .F0(R[12]), .F1(R[13]),
    .S0(SEL[0]), .S1(SEL[1]), .S2(SEL[2]), .B0(Y[12]), .A2(X[14]), .B3(Y[15]), .A3(X[15]), .A0(X[12]),
    .Cin(alu_carry_lookahead_generator_1_c3), .B1(Y[13]), .A1(X[13]), .B2(Y[14]));  // open: Cout
  SN74F381 sn74f381_8 (
    .F2(R[30]), .F3(R[31]), .Cout(Cout), .F0(R[28]), .F1(R[29]), .S0(SEL[0]), .S1(SEL[1]), .S2(SEL[2]),
    .B0(Y[28]), .A2(X[30]), .B3(Y[31]), .A3(X[31]), .A0(X[28]), .Cin(alu_carry_lookahead_generator_1_c7),
    .B1(Y[29]), .A1(X[29]), .B2(Y[30]));  // open: Pbar, Gbar
  LED F_Cout (.in(Cout));

  // Other names for the same wires on the sheet: S[2:0] = SEL
endmodule

module alu_barrel_shifter (
  input  [31:0] X,
  input  nLOGIC_ARITH,
  input  nLEFT_RIGHT,
  input  [4:0] Y,
  output [31:0] R
);

  wire decoder_1_out0, decoder_1_out1, decoder_2_out0, decoder_2_out1, decoder_3_out0, decoder_3_out1,
       decoder_4_out0, decoder_4_out1, decoder_5_out0, decoder_5_out1, not_1_out, not_2_out, not_3_out,
       not_4_out, not_5_out;
  wire [7:0] bit_extender_1_out;
  wire [15:0] bit_extender_2_out;
  wire [31:0] controlled_buffer_1_out, controlled_buffer_4_out, controlled_buffer_7_out,
       controlled_buffer_10_out;
  wire [31:31] and_1_out;

  and and_1 (and_1_out[31], X[31], nLOGIC_ARITH);
  assign controlled_buffer_1_out = decoder_1_out0 ? {X[30:0], 1'b0} : 32'bz;  // Controlled_Buffer controlled_buffer_1
  assign controlled_buffer_1_out = not_1_out ? X : 32'bz;  // Controlled_Buffer controlled_buffer_2
  assign controlled_buffer_1_out = decoder_1_out1 ? {and_1_out[31], X[31:1]} : 32'bz;  // Controlled_Buffer controlled_buffer_3
  not not_1 (not_1_out, Y[0]);
  Decoder decoder_1 (.out0(decoder_1_out0), .out1(decoder_1_out1), .sel(nLEFT_RIGHT), .en(Y[0]));
  assign controlled_buffer_4_out = decoder_2_out0 ? {controlled_buffer_1_out[29:0], 2'b00} : 32'bz;  // Controlled_Buffer controlled_buffer_4
  assign controlled_buffer_4_out = not_2_out ? controlled_buffer_1_out : 32'bz;  // Controlled_Buffer controlled_buffer_5
  assign controlled_buffer_4_out = decoder_2_out1 ? {{2{and_1_out[31]}}, controlled_buffer_1_out[31:2]} : 32'bz;  // Controlled_Buffer controlled_buffer_6
  not not_2 (not_2_out, Y[1]);
  Decoder decoder_2 (.out0(decoder_2_out0), .out1(decoder_2_out1), .sel(nLEFT_RIGHT), .en(Y[1]));
  assign controlled_buffer_7_out = not_3_out ? controlled_buffer_4_out : 32'bz;  // Controlled_Buffer controlled_buffer_7
  assign controlled_buffer_7_out = decoder_3_out1 ? {{4{and_1_out[31]}}, controlled_buffer_4_out[31:4]} : 32'bz;  // Controlled_Buffer controlled_buffer_8
  not not_3 (not_3_out, Y[2]);
  assign controlled_buffer_7_out = decoder_3_out0 ? {controlled_buffer_4_out[27:0], 4'b0000} : 32'bz;  // Controlled_Buffer controlled_buffer_9
  Decoder decoder_3 (.out0(decoder_3_out0), .out1(decoder_3_out1), .sel(nLEFT_RIGHT), .en(Y[2]));
  assign bit_extender_1_out = {{7{and_1_out[31]}}, and_1_out[31]};  // Bit_Extender bit_extender_1
  assign controlled_buffer_10_out = decoder_4_out0 ? {controlled_buffer_7_out[23:0], {8{1'b0}}} : 32'bz;  // Controlled_Buffer controlled_buffer_10
  assign controlled_buffer_10_out = not_4_out ? controlled_buffer_7_out : 32'bz;  // Controlled_Buffer controlled_buffer_11
  assign controlled_buffer_10_out = decoder_4_out1 ? {bit_extender_1_out, controlled_buffer_7_out[31:8]} : 32'bz;  // Controlled_Buffer controlled_buffer_12
  not not_4 (not_4_out, Y[3]);
  Decoder decoder_4 (.out0(decoder_4_out0), .out1(decoder_4_out1), .sel(nLEFT_RIGHT), .en(Y[3]));
  assign R = not_5_out ? controlled_buffer_10_out : 32'bz;  // Controlled_Buffer controlled_buffer_13
  assign bit_extender_2_out = {{15{and_1_out[31]}}, and_1_out[31]};  // Bit_Extender bit_extender_2
  not not_5 (not_5_out, Y[4]);
  assign R = decoder_5_out0 ? {controlled_buffer_10_out[15:0], {16{1'b0}}} : 32'bz;  // Controlled_Buffer controlled_buffer_14
  assign R = decoder_5_out1 ? {bit_extender_2_out, controlled_buffer_10_out[31:16]} : 32'bz;  // Controlled_Buffer controlled_buffer_15
  Decoder decoder_5 (.out0(decoder_5_out0), .out1(decoder_5_out1), .sel(nLEFT_RIGHT), .en(Y[4]));
endmodule

module alu_carry_lookahead_generator (
  input  C0,
  input  P0,
  input  G0,
  input  P1,
  input  G1,
  input  P2,
  input  G2,
  input  P3,
  input  G3,
  input  P4,
  input  G4,
  input  P5,
  input  G5,
  input  P6,
  input  G6,
  output C1,
  output C2,
  output C3,
  output C4,
  output C5,
  output C6,
  output C7
);

  wire and_1_out, and_2_out, and_3_out, and_4_out, and_5_out, and_6_out, and_7_out, and_8_out, and_9_out,
       and_10_out, and_11_out, and_12_out, and_13_out, and_14_out, and_15_out, and_16_out, and_17_out,
       and_18_out, and_19_out, and_20_out, and_21_out, and_22_out, and_23_out, and_24_out, and_25_out,
       and_26_out, and_27_out, and_28_out, not_1_out, not_2_out, not_3_out, not_4_out, not_5_out, not_6_out,
       not_7_out, not_8_out, not_9_out, not_10_out, not_11_out, not_12_out, not_13_out, not_14_out;

  not not_1 (not_1_out, P0);
  not not_2 (not_2_out, G0);
  not not_3 (not_3_out, P1);
  not not_4 (not_4_out, G1);
  not not_5 (not_5_out, P2);
  not not_6 (not_6_out, G2);
  not not_7 (not_7_out, P3);
  not not_8 (not_8_out, G3);
  not not_9 (not_9_out, P4);
  not not_10 (not_10_out, G4);
  not not_11 (not_11_out, P5);
  not not_12 (not_12_out, G5);
  not not_13 (not_13_out, P6);
  not not_14 (not_14_out, G6);
  and and_1 (and_1_out, C0, not_1_out);
  and and_2 (and_2_out, C0, not_1_out, not_3_out);
  and and_3 (and_3_out, not_2_out, not_3_out);
  and and_4 (and_4_out, C0, not_1_out, not_3_out, not_5_out);
  and and_5 (and_5_out, not_2_out, not_3_out, not_5_out);
  and and_6 (and_6_out, not_4_out, not_5_out);
  and and_7 (and_7_out, C0, not_1_out, not_3_out, not_5_out, not_7_out);
  and and_8 (and_8_out, not_2_out, not_3_out, not_5_out, not_7_out);
  and and_9 (and_9_out, not_4_out, not_5_out, not_7_out);
  and and_10 (and_10_out, not_6_out, not_7_out);
  and and_11 (and_11_out, C0, not_1_out, not_3_out, not_5_out, not_7_out, not_9_out);
  and and_12 (and_12_out, not_2_out, not_3_out, not_5_out, not_7_out, not_9_out);
  and and_13 (and_13_out, not_4_out, not_5_out, not_7_out, not_9_out);
  and and_14 (and_14_out, not_6_out, not_7_out, not_9_out);
  and and_15 (and_15_out, not_8_out, not_9_out);
  and and_16 (and_16_out, C0, not_1_out, not_3_out, not_5_out, not_7_out, not_9_out, not_11_out);
  and and_17 (and_17_out, not_2_out, not_3_out, not_5_out, not_7_out, not_9_out, not_11_out);
  and and_18 (and_18_out, not_4_out, not_5_out, not_7_out, not_9_out, not_11_out);
  and and_19 (and_19_out, not_6_out, not_7_out, not_9_out, not_11_out);
  and and_20 (and_20_out, not_8_out, not_9_out, not_11_out);
  and and_21 (and_21_out, not_10_out, not_11_out);
  and and_22 (and_22_out, C0, not_1_out, not_3_out, not_5_out, not_7_out, not_9_out, not_11_out, not_13_out);
  and and_23 (and_23_out, not_2_out, not_3_out, not_5_out, not_7_out, not_9_out, not_11_out, not_13_out);
  and and_24 (and_24_out, not_4_out, not_5_out, not_7_out, not_9_out, not_11_out, not_13_out);
  and and_25 (and_25_out, not_6_out, not_7_out, not_9_out, not_11_out, not_13_out);
  and and_26 (and_26_out, not_8_out, not_9_out, not_11_out, not_13_out);
  and and_27 (and_27_out, not_10_out, not_11_out, not_13_out);
  and and_28 (and_28_out, not_12_out, not_13_out);
  or or_1 (C1, and_1_out, not_2_out);
  or or_2 (C2, and_2_out, and_3_out, not_4_out);
  or or_3 (C3, and_4_out, and_5_out, and_6_out, not_6_out);
  or or_4 (C4, and_7_out, and_8_out, and_9_out, and_10_out, not_8_out);
  or or_5 (C5, and_11_out, and_12_out, and_13_out, and_14_out, and_15_out, not_10_out);
  or or_6 (C6, and_16_out, and_17_out, and_18_out, and_19_out, and_20_out, and_21_out, not_12_out);
  or or_7 (C7, and_22_out, and_23_out, and_24_out, and_25_out, and_26_out, and_27_out, and_28_out, not_14_out);
endmodule

module SN74F381 (
  input  Cin,
  input  B0,
  input  A0,
  input  B1,
  input  A1,
  input  B2,
  input  A2,
  input  B3,
  input  A3,
  input  S0,
  input  S1,
  input  S2,
  output F0,
  output F1,
  output F2,
  output F3,
  output Pbar,
  output Gbar,
  output Cout
);

  wire and_1_out, and_2_out, and_3_out, and_4_out, and_5_out, and_6_out, and_7_out, and_8_out, and_9_out,
       and_10_out, and_11_out, and_12_out, and_13_out, and_14_out, and_15_out, and_16_out, and_17_out,
       and_18_out, and_19_out, and_20_out, and_21_out, and_22_out, and_23_out, and_24_out, and_25_out,
       and_26_out, and_27_out, and_28_out, and_29_out, and_30_out, and_31_out, and_32_out, and_33_out,
       and_34_out, and_35_out, and_36_out, and_37_out, and_38_out, and_39_out, and_40_out, and_41_out,
       and_42_out, and_43_out, and_44_out, nand_1_out, nand_2_out, nand_3_out, nand_4_out, nand_6_out,
       nand_7_out, nor_1_out, nor_2_out, nor_3_out, nor_4_out, nor_5_out, nor_6_out, nor_7_out, nor_8_out,
       nor_9_out, nor_10_out, nor_11_out, nor_12_out, nor_13_out, not_1_out, not_2_out, not_3_out, not_4_out,
       not_5_out, not_6_out, not_7_out, not_8_out, not_9_out, not_10_out, not_11_out, not_12_out, not_13_out,
       not_14_out;

  not not_1 (not_1_out, S0);
  not not_2 (not_2_out, not_1_out);
  not not_3 (not_3_out, S1);
  not not_4 (not_4_out, not_3_out);
  not not_5 (not_5_out, S2);
  not not_6 (not_6_out, B0);
  not not_7 (not_7_out, A0);
  not not_8 (not_8_out, B1);
  not not_9 (not_9_out, A1);
  not not_10 (not_10_out, B2);
  not not_11 (not_11_out, A2);
  not not_12 (not_12_out, B3);
  not not_13 (not_13_out, A3);
  nand nand_1 (nand_1_out, not_1_out, not_3_out);
  nand nand_2 (nand_2_out, not_3_out, not_5_out);
  not not_14 (not_14_out, not_5_out);
  and and_1 (and_1_out, not_7_out, not_6_out, nand_3_out, nand_2_out);
  and and_2 (and_2_out, nand_1_out, nand_3_out, nand_4_out, not_6_out, A0);
  and and_3 (and_3_out, nand_2_out, nand_4_out, B0, not_7_out);
  and and_4 (and_4_out, not_7_out, not_6_out, nand_1_out, nand_4_out, nor_10_out);
  and and_5 (and_5_out, nand_2_out, nand_3_out, not_6_out, A0);
  and and_6 (and_6_out, nand_2_out, nand_3_out, B0, not_7_out);
  and and_7 (and_7_out, nand_1_out, nand_4_out, B0, A0);
  and and_8 (and_8_out, not_9_out, not_8_out, nand_3_out, nand_2_out);
  and and_9 (and_9_out, nand_1_out, nand_3_out, nand_4_out, not_8_out, A1);
  and and_10 (and_10_out, nand_2_out, nand_4_out, B1, not_9_out);
  and and_11 (and_11_out, not_9_out, not_8_out, nand_1_out, nand_4_out, nor_10_out);
  and and_12 (and_12_out, nand_2_out, nand_3_out, not_8_out, A1);
  and and_13 (and_13_out, nand_2_out, nand_3_out, B1, not_9_out);
  and and_14 (and_14_out, nand_1_out, nand_4_out, B1, A1);
  and and_15 (and_15_out, not_11_out, not_10_out, nand_3_out, nand_2_out);
  and and_16 (and_16_out, nand_1_out, nand_3_out, nand_4_out, not_10_out, A2);
  and and_17 (and_17_out, nand_2_out, nand_4_out, B2, not_11_out);
  and and_18 (and_18_out, not_11_out, not_10_out, nand_1_out, nand_4_out, nor_10_out);
  and and_19 (and_19_out, nand_2_out, nand_3_out, not_10_out, A2);
  and and_20 (and_20_out, nand_2_out, nand_3_out, B2, not_11_out);
  and and_21 (and_21_out, nand_1_out, nand_4_out, B2, A2);
  and and_22 (and_22_out, not_13_out, not_12_out, nand_3_out, nand_2_out);
  and and_23 (and_23_out, nand_1_out, nand_3_out, nand_4_out, not_12_out, A3);
  and and_24 (and_24_out, nand_2_out, nand_4_out, B3, not_13_out);
  and and_25 (and_25_out, not_13_out, not_12_out, nand_1_out, nand_4_out, nor_10_out);
  and and_26 (and_26_out, nand_2_out, nand_3_out, not_12_out, A3);
  and and_27 (and_27_out, nand_2_out, nand_3_out, B3, not_13_out);
  and and_28 (and_28_out, nand_1_out, nand_4_out, B3, A3);
  and and_29 (and_29_out, not_1_out, not_3_out);
  nand nand_3 (nand_3_out, not_1_out, not_4_out);
  nand nand_4 (nand_4_out, not_2_out, not_4_out, not_5_out);
  and and_30 (and_30_out, not_3_out, not_14_out);
  nor nor_1 (nor_1_out, and_1_out, and_2_out, and_3_out);
  nor nor_2 (nor_2_out, and_4_out, and_5_out, and_6_out, and_7_out);
  nor nor_3 (nor_3_out, and_8_out, and_9_out, and_10_out);
  nor nor_4 (nor_4_out, and_11_out, and_12_out, and_13_out, and_14_out);
  nor nor_5 (nor_5_out, and_15_out, and_16_out, and_17_out);
  nor nor_6 (nor_6_out, and_18_out, and_19_out, and_20_out, and_21_out);
  nor nor_7 (nor_7_out, and_22_out, and_23_out, and_24_out);
  nor nor_8 (nor_8_out, and_25_out, and_26_out, and_27_out, and_28_out);
  nor nor_9 (nor_9_out, and_29_out, not_14_out);
  and and_31 (and_31_out, not_1_out, not_14_out);
  nor nor_10 (nor_10_out, and_31_out, and_30_out);
  and and_32 (and_32_out, Cin, nor_1_out, nor_9_out);
  and and_33 (and_33_out, nor_1_out, nor_2_out, nor_9_out);
  and and_34 (and_34_out, Cin, nor_1_out, nor_3_out, nor_9_out);
  and and_35 (and_35_out, nor_1_out, nor_3_out, nor_2_out, nor_9_out);
  and and_36 (and_36_out, nor_3_out, nor_4_out, nor_9_out);
  and and_37 (and_37_out, Cin, nor_1_out, nor_3_out, nor_5_out, nor_9_out);
  and and_38 (and_38_out, nor_1_out, nor_3_out, nor_5_out, nor_2_out, nor_9_out);
  and and_39 (and_39_out, nor_3_out, nor_5_out, nor_4_out, nor_9_out);
  and and_40 (and_40_out, nor_5_out, nor_6_out, nor_9_out);
  nand nand_5 (Pbar, nor_1_out, nor_3_out, nor_5_out, nor_7_out);
  and and_41 (and_41_out, nor_1_out, nor_3_out, nor_5_out, nor_7_out, nor_2_out);
  and and_42 (and_42_out, nor_3_out, nor_5_out, nor_7_out, nor_4_out);
  and and_43 (and_43_out, nor_5_out, nor_7_out, nor_6_out);
  and and_44 (and_44_out, nor_7_out, nor_8_out);
  nand nand_6 (nand_6_out, Cin, nor_1_out, nor_3_out, nor_5_out, nor_7_out);
  nand nand_7 (nand_7_out, Cin, nor_9_out);
  nor nor_11 (nor_11_out, and_32_out, and_33_out);
  nor nor_12 (nor_12_out, and_34_out, and_35_out, and_36_out);
  nor nor_13 (nor_13_out, and_37_out, and_38_out, and_39_out, and_40_out);
  nor nor_14 (Gbar, and_41_out, and_42_out, and_43_out, and_44_out);
  xor xor_1 (F0, nand_7_out, nor_2_out);
  xor xor_2 (F1, nor_11_out, nor_4_out);
  xor xor_3 (F2, nor_12_out, nor_6_out);
  xor xor_4 (F3, nor_13_out, nor_8_out);
  nand nand_8 (Cout, Gbar, nand_6_out);
endmodule

module SN74AS885 (
  input  [7:0] P,
  input  PLE,
  input  [7:0] Q,
  input  P_gt_Q_in,
  input  P_lt_Q_in,
  input  LAn,
  output P_lt_Q,
  output P_gt_Q
);

  wire and_1_out, and_2_out, and_3_out, and_4_out, and_5_out, and_6_out, and_7_out, and_8_out, and_9_out,
       and_10_out, and_11_out, and_12_out, and_13_out, and_14_out, and_15_out, and_16_out, and_17_out,
       and_18_out, and_19_out, and_20_out, and_21_out, and_22_out, and_23_out, and_24_out, and_25_out,
       and_26_out, and_27_out, and_28_out, and_29_out, and_30_out, and_31_out, and_32_out, and_33_out,
       and_34_out, and_35_out, and_36_out, and_37_out, and_38_out, and_39_out, and_40_out, and_41_out,
       and_42_out, nor_1_out, nor_2_out, nor_3_out, nor_4_out, nor_5_out, nor_6_out, nor_7_out, nor_8_out,
       nor_9_out, nor_10_out, nor_11_out, nor_12_out, not_1_out, not_2_out, not_3_out, not_4_out, not_5_out,
       not_6_out, not_7_out, not_8_out, not_9_out, not_10_out, not_11_out, not_12_out, not_13_out,
       not_14_out, not_15_out, not_16_out, not_17_out;
  wire [7:0] register_1_q;

  Register #(.trigger("high")) register_1 (.D(P), .clk(PLE), .Q(register_1_q));  // open: en, clr
  not not_1 (not_1_out, register_1_q[7]);
  not not_2 (not_2_out, register_1_q[6]);
  not not_3 (not_3_out, register_1_q[5]);
  not not_4 (not_4_out, register_1_q[4]);
  not not_5 (not_5_out, register_1_q[3]);
  not not_6 (not_6_out, register_1_q[2]);
  not not_7 (not_7_out, register_1_q[1]);
  not not_8 (not_8_out, register_1_q[0]);
  not not_9 (not_9_out, Q[7]);
  not not_10 (not_10_out, Q[6]);
  not not_11 (not_11_out, Q[5]);
  not not_12 (not_12_out, Q[4]);
  not not_13 (not_13_out, Q[3]);
  not not_14 (not_14_out, Q[2]);
  not not_15 (not_15_out, Q[1]);
  not not_16 (not_16_out, Q[0]);
  not not_17 (not_17_out, LAn);
  and and_1 (and_1_out, not_9_out, register_1_q[7]);
  and and_2 (and_2_out, Q[7], not_1_out);
  and and_3 (and_3_out, not_10_out, register_1_q[6]);
  and and_4 (and_4_out, Q[6], not_2_out);
  and and_5 (and_5_out, not_11_out, register_1_q[5]);
  and and_6 (and_6_out, Q[5], not_3_out);
  and and_7 (and_7_out, not_13_out, register_1_q[3]);
  and and_8 (and_8_out, Q[3], not_5_out);
  and and_9 (and_9_out, not_14_out, register_1_q[2]);
  and and_10 (and_10_out, Q[2], not_6_out);
  and and_11 (and_11_out, register_1_q[1], not_15_out);
  and and_12 (and_12_out, Q[1], not_7_out);
  and and_13 (and_13_out, register_1_q[0], not_16_out);
  and and_14 (and_14_out, Q[0], not_8_out);
  nor nor_1 (nor_1_out, and_1_out, and_2_out);
  nor nor_2 (nor_2_out, and_3_out, and_4_out);
  nor nor_3 (nor_3_out, and_5_out, and_6_out);
  nor nor_4 (nor_4_out, and_7_out, and_8_out);
  nor nor_5 (nor_5_out, and_9_out, and_10_out);
  nor nor_6 (nor_6_out, and_11_out, and_12_out);
  nor nor_7 (nor_7_out, and_13_out, and_14_out);
  and and_15 (and_15_out, register_1_q[7], not_9_out);
  and and_16 (and_16_out, not_1_out, Q[7]);
  and and_17 (and_17_out, register_1_q[6], not_10_out);
  and and_18 (and_18_out, not_2_out, Q[6]);
  and and_19 (and_19_out, register_1_q[5], not_11_out);
  and and_20 (and_20_out, not_3_out, Q[5]);
  and and_21 (and_21_out, not_12_out, register_1_q[4]);
  and and_22 (and_22_out, Q[4], not_4_out);
  nor nor_8 (nor_8_out, and_15_out, and_16_out, and_17_out, and_18_out, and_19_out, and_20_out, and_21_out, and_22_out);
  and and_23 (and_23_out, register_1_q[7], not_16_out, not_17_out);
  and and_24 (and_24_out, not_1_out, Q[7], LAn);
  and and_25 (and_25_out, not_2_out, Q[6], nor_1_out);
  and and_26 (and_26_out, not_3_out, Q[5], nor_1_out, nor_2_out);
  and and_27 (and_27_out, not_4_out, Q[4], nor_1_out, nor_2_out, nor_3_out);
  and and_28 (and_28_out, not_5_out, Q[3], nor_8_out);
  and and_29 (and_29_out, not_6_out, Q[2], nor_8_out, nor_4_out);
  and and_30 (and_30_out, not_7_out, Q[1], nor_8_out, nor_4_out, nor_5_out);
  and and_31 (and_31_out, not_8_out, Q[0], nor_8_out, nor_4_out, nor_5_out, nor_6_out);
  and and_32 (and_32_out, nor_8_out, nor_4_out, nor_5_out, nor_6_out, nor_7_out, P_lt_Q_in);
  and and_33 (and_33_out, register_1_q[7], not_9_out, LAn);
  and and_34 (and_34_out, not_1_out, Q[7], not_17_out);
  and and_35 (and_35_out, register_1_q[6], not_10_out, nor_1_out);
  and and_36 (and_36_out, register_1_q[5], not_11_out, nor_1_out, nor_2_out);
  and and_37 (and_37_out, register_1_q[4], not_12_out, nor_1_out, nor_2_out, nor_3_out);
  and and_38 (and_38_out, register_1_q[3], not_13_out, nor_8_out);
  and and_39 (and_39_out, register_1_q[2], not_14_out, nor_4_out, nor_8_out);
  and and_40 (and_40_out, not_15_out, register_1_q[1], nor_8_out, nor_4_out, nor_5_out);
  and and_41 (and_41_out, not_16_out, register_1_q[0], nor_8_out, nor_4_out, nor_5_out, nor_6_out);
  and and_42 (and_42_out, nor_8_out, nor_4_out, nor_5_out, nor_6_out, nor_7_out, P_gt_Q_in);
  nor nor_9 (nor_9_out, and_23_out, and_24_out, and_25_out, and_26_out, and_27_out);
  nor nor_10 (nor_10_out, and_28_out, and_29_out, and_30_out, and_31_out, and_32_out);
  nor nor_11 (nor_11_out, and_33_out, and_34_out, and_35_out, and_36_out, and_37_out);
  nor nor_12 (nor_12_out, and_38_out, and_39_out, and_40_out, and_41_out, and_42_out);
  nand nand_1 (P_lt_Q, nor_9_out, nor_10_out);
  nand nand_2 (P_gt_Q, nor_11_out, nor_12_out);
endmodule

module IDT7216 (
  input  [15:0] X,
  input  OELn,
  input  CLK_XY,
  input  [15:0] Yin,
  output [15:0] Yout,
  output [15:0] P
);

  wire not_1_out;
  wire [15:0] multiplier_1_out, register_1_q, register_2_q;

  Register #(.width(16)) register_1 (.D(X), .clk(CLK_XY), .Q(register_1_q));  // open: en, clr
  Register #(.width(16)) register_2 (.D(Yin), .clk(CLK_XY), .Q(register_2_q));  // open: en, clr
  Multiplier #(.width(16)) multiplier_1 (
    .a(register_1_q), .b(register_2_q), .out(multiplier_1_out), .cout(P));  // open: cin
  not not_1 (not_1_out, OELn);
  assign Yout = not_1_out ? multiplier_1_out : 16'bz;  // Controlled_Buffer controlled_buffer_1
endmodule
