// Logisim project ImmDecoder.circ as structural Verilog: 1 circuit, main circuit main
module main (
);

  wire button_1_out, button_2_out, nand_1_out, or_1_out, P7, P20, P31, S4_1_0, S4_1_1, S10_5, S19_12, S30_20,
       X0, X11, X31;
  wire [0:0] IMM_p3;
  wire [1:0] rom_1_data;
  wire [2:0] and_3_out, multiplexer_2_out_3;
  wire [3:0] and_1_out, and_2_out, multiplexer_1_out, multiplexer_1_out_2, multiplexer_2_out,
       multiplexer_2_out_2, or_2_out_2, P11_8;
  wire [3:1] or_2_out;
  wire [4:0] OP;
  wire [4:1] P24_20;
  wire [5:0] CLF_p3, P30_25;
  wire [7:0] counter_1_q, P19_12;

  LED led_1 (.in(OP[4]));
  LED led_2 (.in(OP[3]));
  LED led_3 (.in(OP[2]));
  LED led_4 (.in(P11_8[3]));
  LED led_5 (.in(P11_8[2]));
  LED led_6 (.in(P11_8[1]));
  LED led_7 (.in(P19_12[2]));
  LED led_8 (.in(P19_12[1]));
  LED led_9 (.in(P19_12[0]));
  LED led_10 (.in(P19_12[7]));
  LED led_11 (.in(P19_12[6]));
  LED led_12 (.in(P19_12[5]));
  LED led_13 (.in(P24_20[4]));
  LED led_14 (.in(P24_20[3]));
  LED led_15 (.in(P24_20[2]));
  LED led_16 (.in(P31));
  LED led_17 (.in(P30_25[5]));
  LED led_18 (.in(P30_25[4]));
  Button button_1 (.out(button_1_out));
  Button button_2 (.out(button_2_out));
  nand nand_1 (nand_1_out, rom_1_data[0], rom_1_data[1]);
  LED led_19 (.in(OP[1]));
  LED led_20 (.in(OP[0]));
  LED led_21 (.in(P11_8[0]));
  LED led_22 (.in(P7));
  LED led_23 (.in(P19_12[4]));
  LED led_24 (.in(P19_12[3]));
  LED led_25 (.in(P24_20[1]));
  LED led_26 (.in(P20));
  LED led_27 (.in(P30_25[3]));
  LED led_28 (.in(P30_25[2]));
  LED led_29 (.in(P30_25[1]));
  LED led_30 (.in(P30_25[0]));
  Counter counter_1 (.clr(button_1_out), .clk(button_2_out), .Q(counter_1_q));  // open: load, up, count, D, carry
  LED led_31 (.in(or_1_out));
  or or_1 (or_1_out, nand_1_out, IMM_p3[0]);
  ROM #(.dataWidth(32)) rom_1 (
    .addr(counter_1_q), .data({P31, P30_25, P24_20, P20, P19_12, P11_8, P7, OP, rom_1_data}));
  assign and_1_out = {4{S4_1_1}} & P11_8;  // AND_Gate and_1, 4 bits wide
  assign and_2_out = {4{S4_1_0}} & P24_20;  // AND_Gate and_2, 4 bits wide
  assign {and_3_out, or_2_out_2[3:1]} = {6{S10_5}} & P30_25;  // AND_Gate and_3, 6 bits wide
  Multiplexer #(.enable("false"), .width(8)) multiplexer_1 (
    .in0({8{X31}}), .in1(P19_12), .out({multiplexer_1_out_2, multiplexer_1_out}), .sel(S19_12));
  Multiplexer #(.enable("false"), .width(11)) multiplexer_2 (
    .in0({11{X31}}), .in1({P30_25, P24_20, P20}),
    .out({multiplexer_2_out_3, multiplexer_2_out_2, multiplexer_2_out}), .sel(S30_20));
  assign {or_2_out_2[0], or_2_out} = and_1_out | and_2_out;  // OR_Gate or_2, 4 bits wide
  LED led_32 (.in(multiplexer_2_out_3[2]));
  LED led_33 (.in(multiplexer_2_out_3[1]));
  LED led_34 (.in(X31));
  // PlaRom #(.Contents("0 0 2 1 2 1*3 0 2 0 2*3 1 1 0 2 0 2 2 1 1 2 0 2 0 1*3 2 2 0 2 0 1 1 0 1 1 0*3 2*3 1 1 0*3 2 2 1 0 2 0*3 1*3 2 2 0*3 1 1 0 1 1 0*4 2 1*3 0*3 2 0*8 1 0 0 1 0*5 1 0*8 2 0*3 2*3 1*3 0 2 0 2 2 1 2*3 0 0 2 0*4 2 0*3 1 0 0 1 2 0*4 1 0 0 2 0*5 2 0*4 1 0 2 1 2 0*3 2 2 1 2*3 0*3 1 0*3 2 0*6 2 0*3 2 1 0*6 2 0 2 0 2 0*3 1 2 1 0 2 0*3 1 0 1 1 2 0*5 2 2 0*7 2 1 1 0*8 1 0*8 1 0*8 1 0*8 1 0*9 1 0*8 1 0*8 1 0*8 1 0*9 1 0*9 1 0*8 1 0*8 1 0*8 1 0*9 1 0*8 1 0*8 1 0 0 1 0*5 1 0*8 1 0 0 1 0*5 1 0 0 1 0*6 1 1 0*7 1 0*10 1 0*8 1 0*9 1 0*8 1 0*8 1 0*8 1 0*8 1 0*8 1"), .\and (30), .outputs(9)) IMM: pin names not known; wires that end beside it: {P31, P20, P7, OP}, 1'b0, {X0, S4_1_0, S4_1_1, S10_5, X11, S19_12, S30_20, X31, IMM_p3[0]}
  Hex_Digit_Display hex_digit_display_1 (.value({X31, multiplexer_2_out_3}));  // open: dp
  LED led_35 (.in(multiplexer_2_out_3[0]));
  LED led_36 (.in(multiplexer_2_out_2[3]));
  LED led_37 (.in(multiplexer_2_out_2[2]));
  LED led_38 (.in(multiplexer_2_out_2[1]));
  Hex_Digit_Display hex_digit_display_2 (.value(multiplexer_2_out_2));  // open: dp
  Hex_Digit_Display hex_digit_display_3 (.value(multiplexer_2_out));  // open: dp
  LED led_39 (.in(multiplexer_2_out_2[0]));
  LED led_40 (.in(multiplexer_2_out[3]));
  LED led_41 (.in(multiplexer_2_out[2]));
  LED led_42 (.in(multiplexer_2_out[1]));
  Hex_Digit_Display hex_digit_display_4 (.value(multiplexer_1_out_2));  // open: dp
  Hex_Digit_Display hex_digit_display_5 (.value(multiplexer_1_out));  // open: dp
  LED led_43 (.in(multiplexer_2_out[0]));
  LED led_44 (.in(multiplexer_1_out_2[3]));
  LED led_45 (.in(multiplexer_1_out_2[2]));
  LED led_46 (.in(multiplexer_1_out_2[1]));
  // PlaRom #(.Contents("1 2 2 1*4 0 1*5 2*4 1 1 2*4 1*3 2 1*3 2 2 1*4 0 2 1 2*3 1 2*3 1 0*3 2 0 2 0 2 1 2 1 0 2 1 0 1 1 2 0 0 2 2 0*4 2 1 1 0*6 1 0*5 1 0*5 1 0*5 1 0*6 1 0*6 1 0*6 1 0*6 1 0*36"), .\and (15), .outputs(6)) CLF: pin names not known; wires that end beside it: OP, 1'b0, CLF_p3
  Hex_Digit_Display hex_digit_display_6 (.value({X11, and_3_out}));  // open: dp
  Hex_Digit_Display hex_digit_display_7 (.value(or_2_out_2));  // open: dp
  LED led_47 (.in(multiplexer_1_out_2[0]));
  LED led_48 (.in(multiplexer_1_out[3]));
  LED led_49 (.in(multiplexer_1_out[2]));
  LED led_50 (.in(multiplexer_1_out[1]));
  Hex_Digit_Display hex_digit_display_8 (.value({or_2_out, X0}));  // open: dp
  LED led_51 (.in(multiplexer_1_out[0]));
  LED led_52 (.in(X11));
  LED led_53 (.in(and_3_out[2]));
  LED led_54 (.in(and_3_out[1]));
  LED led_55 (.in(CLF_p3[0]));
  LED led_56 (.in(CLF_p3[1]));
  LED led_57 (.in(CLF_p3[2]));
  LED led_58 (.in(CLF_p3[3]));
  LED led_59 (.in(CLF_p3[4]));
  LED led_60 (.in(CLF_p3[5]));
  LED led_61 (.in(and_3_out[0]));
  LED led_62 (.in(or_2_out_2[3]));
  LED led_63 (.in(or_2_out_2[2]));
  LED led_64 (.in(or_2_out_2[1]));
  LED led_65 (.in(or_2_out_2[0]));
  LED led_66 (.in(or_2_out[3]));
  LED led_67 (.in(or_2_out[2]));
  LED led_68 (.in(or_2_out[1]));
  LED led_69 (.in(X0));

  // Other names for the same wires on the sheet: P24_21[3:0] = P24_20; P24_20[0] = P20

  // Notes on the sheet:
  //   funct3/imm
  //   rs1/imm
  //   rs2/imm
  //   funct7/imm
  //   2'b11
  //   OP
  //   rd/imm
  //   SIGILL
  //   contents of rom_1 (hex, n*v repeats v):
  //   fe010113 812e23 2010413 17b7 23478793 fef42623 fec42703 27b7 34478793 e7e863 fec42783 a78793
  //   fef42623 fec42703 8abcd7b7 f707b3 78713 fec42783 ab78793 f72023 fec42783 178793 fef42623 fbdff06f
  //   ILL
  //   X31
  //   S[30:20]
  //   S[19:12]
  //   X11
  //   S[10:5]
  //   S[4:1].1
  //   S[4:1].0
  //   X0
  //   J
  //   U
  //   B
  //   S
  //   I
  //   R
endmodule
