// Logisim project Instruction_Decoder.circ as structural Verilog: 1 circuit, main circuit main
module main (
);

  wire nand_1_out;

  LED led_1 (.in(1'b0));
  LED led_2 (.in(1'b0));
  LED led_3 (.in(1'b0));
  LED led_4 (.in(nand_1_out));
  nand nand_1 (nand_1_out, 1'b1, 1'b1);
  LED led_5 (.in(1'b1));
  LED led_6 (.in(1'b0));
  LED led_7 (.in(1'b0));
  LED led_8 (.in(1'b0));
  LED led_9 (.in(1'b1));
  LED led_10 (.in(1'b0));
  LED led_11 (.in(1'b0));
  LED led_12 (.in(1'b0));
  LED led_13 (.in(1'b0));
  LED led_14 (.in(1'b0));
  LED led_15 (.in(1'b0));
  LED led_16 (.in(1'b0));
  LED led_17 (.in(1'b0));
  LED led_18 (.in(1'b1));
  LED led_19 (.in(1'b0));
  LED led_20 (.in(1'b0));
  LED led_21 (.in(1'b0));
  ROM #(.addrWidth(15), .misaligned("true")) rom_1 (.addr(15'h2100));  // open: data
  LED led_22 (.in(1'b0));
  LED led_23 (.in(1'b0));
  LED led_24 (.in(1'b0));
  LED led_25 (.in(1'b1));
  LED led_26 (.in(1'b0));
  LED led_27 (.in(1'b0));
  LED led_28 (.in(1'b0));
  LED led_29 (.in(1'b0));
  LED led_30 (.in(1'b0));
  LED led_31 (.in(1'b0));

  // Notes on the sheet:
  //   2'b11
  //   OP
  //   rd/imm
  //   funct3/imm
  //   rs1/imm
  //   rs2/imm
  //   funct7/imm
  //   SIGILL
endmodule
